// Logisim project Proje.circ as structural Verilog: 31 circuits, main circuit main
module main (
  input  [6:0] \input 
);

  wire ac_controller_1_clear, ac_controller_1_increment, alu_1_e_out, ar_controller_1_clear,
       ar_controller_1_increment, ar_controller_1_load, clk, dr_controller_1_increment, dr_controller_1_load,
       E, e_controller_1_clear, e_controller_1_comp, e_controller_1_load, FGI,
       fgi_fgo_ien_controller_1_fgi_k, fgi_fgo_ien_controller_1_fgo_j, fgi_fgo_ien_controller_1_fgo_k,
       fgi_fgo_ien_controller_1_ien_j, fgi_fgo_ien_controller_1_ien_k, FGO, IEN, ir_controller_1_load,
       not_1_out, out_controller_1_ld, pc_controller_1_clear, pc_controller_1_increment,
       pc_controller_1_load, R, ram_controller_1_load, sc_controller_1_clear, tr_controller_1_load, undriven;
  wire [2:0] bus_select_1_bus_select, T;
  wire [7:0] outr;
  wire [11:0] AR, PC;
  wire [15:0] AC, alu_1_ac_entiry, BUS, DR, IR, Memory_Data, ram_1_data, TR;

  SC_Controller sc_controller_1 (.Clear(sc_controller_1_clear), .T(T), .R(R), .IR(IR));
  ALU alu_1 (.DR(DR), .AC(AC), .E_out(alu_1_e_out), .AC_Entiry(alu_1_ac_entiry), .E_in(E), .T(T), .IR(IR));
  SC sc_1 (.Clock(clk), .out_3(T[2]), .out_5(T[0]), .out_4(T[1]), .CLR(sc_controller_1_clear));
  E_Controller e_controller_1 (
    .Comp(e_controller_1_comp), .Clear(e_controller_1_clear), .Load(e_controller_1_load), .T(T), .IR(IR));
  E e_1 (
    .E_IN(alu_1_e_out), .Comp(e_controller_1_comp), .E_OUT(E), .Clock(clk), .load(e_controller_1_load),
    .Clear(e_controller_1_clear));
  OUT_Controller out_controller_1 (.LD(out_controller_1_ld), .T(T), .IR(IR));
  Clock clock_1 (.out(clk));
  AR_Controller ar_controller_1 (
    .Load(ar_controller_1_load), .Clear(ar_controller_1_clear), .Increment(ar_controller_1_increment), .T(T),
    .R(R), .IR(IR));
  PC_Controller pc_controller_1 (
    .Load(pc_controller_1_load), .Increment(pc_controller_1_increment), .Clear(pc_controller_1_clear), .T(T),
    .FGI(FGI), .FGO(FGO), .E(E), .R(R), .IR(IR), .DR(DR), .AC(AC));
  DR_Controller dr_controller_1 (.Load(dr_controller_1_load), .Increment(dr_controller_1_increment), .T(T), .IR(IR));
  AC_Controller ac_controller_1 (.Clear(ac_controller_1_clear), .Increment(ac_controller_1_increment), .T(T), .IR(IR));
  IR_Controller ir_controller_1 (.Load(ir_controller_1_load), .T(T), .R(R));
  TR_Controller tr_controller_1 (.Load(tr_controller_1_load), .T(T), .R(R));
  OUTR outr_1 (.Clear(1'b0), .Load(out_controller_1_ld), .Clk(clk), .Increment(1'b0), .OUT_in(BUS[7:0]), .OUT(outr));
  RAM #(.addrWidth(12), .dataWidth(16)) ram_1 (
    .addr(AR), .data(ram_1_data), .clk(clk), .ld(ram_controller_1_load));  // open: sel, clr
  AR ar_1 (
    .Clear(ar_controller_1_clear), .Load(ar_controller_1_load), .Incriment(ar_controller_1_increment),
    .BUS_IN(BUS[11:0]), .BUS_OUT(AR), .Clock(clk));
  AC ac_1 (
    .Clear(ac_controller_1_clear), .Load(1'b1), .Incriment(ac_controller_1_increment),
    .ALU_IN(alu_1_ac_entiry), .Clock(clk), .BUS_OUT(AC));
  TR tr_1 (.Clear(1'b0), .Load(tr_controller_1_load), .Incriment(1'b0), .BUS_IN(BUS), .Clock(clk), .BUS_OUT(TR));
  PC pc_1 (
    .BUS_OUT(PC), .BUS_IN(BUS[11:0]), .Clock(clk), .Load(pc_controller_1_load),
    .Incriment(pc_controller_1_increment), .Clear(pc_controller_1_clear));
  DR dr_1 (
    .Clear(1'b0), .Load(dr_controller_1_load), .Incriment(dr_controller_1_increment), .BUS_IN(BUS),
    .Clock(clk), .BUS_OUT(DR));
  IR ir_1 (.Clear(1'b0), .Load(ir_controller_1_load), .Incriment(1'b0), .BUS_IN(BUS), .Clock(clk), .BUS_OUT(IR));
  assign Memory_Data = ram_controller_1_load ? ram_1_data : 16'bz;  // Controlled_Buffer controlled_buffer_1
  RAM_Controller ram_controller_1 (.Load(ram_controller_1_load), .T(T), .R(R), .IR(IR));
  not not_1 (not_1_out, ram_controller_1_load);
  assign ram_1_data = not_1_out ? BUS : 16'bz;  // Controlled_Buffer controlled_buffer_2
  Multiplexer #(.select(3), .width(16), .enable("false")) multiplexer_1 (
    .in1({4'b0000, AR}), .in2({4'b0000, PC}), .in3(DR), .in4(AC), .in5(IR), .in6(TR), .in7(Memory_Data),
    .out(BUS), .sel(bus_select_1_bus_select));  // open: in0
  BUS_Select bus_select_1 (.T(T), .R(R), .IR(IR), .Bus_Select(bus_select_1_bus_select));
  FGI_FGO_IEN_Controller fgi_fgo_ien_controller_1 (
    .FGO_K(fgi_fgo_ien_controller_1_fgo_k), .FGI_K(fgi_fgo_ien_controller_1_fgi_k),
    .IEN_K(fgi_fgo_ien_controller_1_ien_k), .IEN_J(fgi_fgo_ien_controller_1_ien_j),
    .FGO_J(fgi_fgo_ien_controller_1_fgo_j), .T(T), .R(R), .IR(IR));
  Hex_Digit_Display hex_digit_display_1 (.value({1'b0, T}));  // open: dp
  FGO fgo_1 (.FGO_J(fgi_fgo_ien_controller_1_fgo_j), .FGO_K(fgi_fgo_ien_controller_1_fgo_k), .Clock(clk), .FGO(FGO));
  FGI fgi_1 (.FGI_J(undriven), .FGI_K(fgi_fgo_ien_controller_1_fgi_k), .Clock(clk), .FGI(FGI));
  IEN ien_1 (.IEN_J(fgi_fgo_ien_controller_1_ien_j), .Clock(clk), .IEN_K(fgi_fgo_ien_controller_1_ien_k), .IEN(IEN));
  Hex_Digit_Display hex_digit_display_2 (.value(AR[11:8]));  // open: dp
  Hex_Digit_Display hex_digit_display_3 (.value(PC[11:8]));  // open: dp
  Hex_Digit_Display hex_digit_display_4 (.value(DR[15:12]));  // open: dp
  Hex_Digit_Display hex_digit_display_5 (.value(AC[15:12]));  // open: dp
  Hex_Digit_Display hex_digit_display_6 (.value(IR[15:12]));  // open: dp
  Hex_Digit_Display hex_digit_display_7 (.value(TR[15:12]));  // open: dp
  Hex_Digit_Display hex_digit_display_8 (.value(AR[3:0]));  // open: dp
  Hex_Digit_Display hex_digit_display_9 (.value(AR[7:4]));  // open: dp
  Hex_Digit_Display hex_digit_display_10 (.value(PC[7:4]));  // open: dp
  Hex_Digit_Display hex_digit_display_11 (.value(DR[11:8]));  // open: dp
  Hex_Digit_Display hex_digit_display_12 (.value(DR[7:4]));  // open: dp
  Hex_Digit_Display hex_digit_display_13 (.value(AC[7:4]));  // open: dp
  Hex_Digit_Display hex_digit_display_14 (.value(AC[11:8]));  // open: dp
  Hex_Digit_Display hex_digit_display_15 (.value(IR[7:4]));  // open: dp
  Hex_Digit_Display hex_digit_display_16 (.value(IR[11:8]));  // open: dp
  Hex_Digit_Display hex_digit_display_17 (.value(TR[7:4]));  // open: dp
  Hex_Digit_Display hex_digit_display_18 (.value(TR[11:8]));  // open: dp
  R_Controller r_controller_1 (.T(T), .IEN(IEN), .FGO(FGO), .FGI(FGI), .R(R));
  Hex_Digit_Display hex_digit_display_19 (.value(PC[3:0]));  // open: dp
  Hex_Digit_Display hex_digit_display_20 (.value(DR[3:0]));  // open: dp
  Hex_Digit_Display hex_digit_display_21 (.value(AC[3:0]));  // open: dp
  Hex_Digit_Display hex_digit_display_22 (.value(IR[3:0]));  // open: dp
  Hex_Digit_Display hex_digit_display_23 (.value(TR[3:0]));  // open: dp
  Hex_Digit_Display hex_digit_display_24 (.value(outr[7:4]));  // open: dp
  Hex_Digit_Display hex_digit_display_25 (.value(outr[3:0]));  // open: dp
  Hex_Digit_Display hex_digit_display_26 (.value(BUS[15:12]));  // open: dp
  Hex_Digit_Display hex_digit_display_27 (.value(BUS[11:8]));  // open: dp
  Hex_Digit_Display hex_digit_display_28 (.value(BUS[7:4]));  // open: dp
  Hex_Digit_Display hex_digit_display_29 (.value(BUS[3:0]));  // open: dp

  // Other names for the same wires on the sheet: INPUT_t[6:0] = \input 

  // Notes on the sheet:
  //   Bu Proje Sakarya Uygulamalı Bilimler Üniversitesi 
  //   Bilgisayar Mühendisliği Öğrencisi Furkan Duran Tarafından Yapılmıştır.
  //   İletişime geçmek için b210109048@subu.edu.tr mail adresini kullanabilirsiniz
  //   AR
  //   PC
  //   DR
  //   AC
  //   IR
  //   TR
  //   OUTR
  //   BUS
endmodule

module AR (
  input  Clear,
  input  Load,
  input  Incriment,
  input  [11:0] BUS_IN,
  input  Clock,
  output [11:0] BUS_OUT
);

  wire and_1_out, and_2_out, and_3_out, and_4_out, and_5_out, and_6_out, and_7_out, and_8_out, and_9_out,
       and_10_out, and_11_out, and_12_out, and_13_out, and_14_out, and_15_out, and_16_out, and_17_out,
       and_18_out, and_19_out, and_20_out, and_21_out, and_22_out, and_23_out, and_24_out, and_25_out,
       and_26_out, and_27_out, and_28_out, and_29_out, and_30_out, and_31_out, and_32_out, and_33_out,
       and_34_out, and_35_out, and_36_out, and_37_out, and_38_out, not_1_out, not_2_out, not_3_out,
       not_4_out, not_5_out, not_6_out, not_7_out, not_8_out, not_9_out, not_10_out, not_11_out, not_12_out,
       not_13_out, not_14_out, or_1_out, or_2_out, or_3_out, or_4_out, or_5_out, or_6_out, or_7_out,
       or_8_out, or_9_out, or_10_out, or_11_out, or_12_out, or_13_out, or_14_out, or_15_out, or_16_out,
       or_17_out, or_18_out, or_19_out, or_20_out, or_21_out, or_22_out, or_23_out, or_24_out;

  not not_1 (not_1_out, Clear);
  not not_2 (not_2_out, Load);
  not not_3 (not_3_out, BUS_IN[0]);
  not not_4 (not_4_out, BUS_IN[1]);
  not not_5 (not_5_out, BUS_IN[2]);
  not not_6 (not_6_out, BUS_IN[3]);
  not not_7 (not_7_out, BUS_IN[4]);
  not not_8 (not_8_out, BUS_IN[5]);
  not not_9 (not_9_out, BUS_IN[6]);
  not not_10 (not_10_out, BUS_IN[7]);
  not not_11 (not_11_out, BUS_IN[8]);
  not not_12 (not_12_out, BUS_IN[9]);
  not not_13 (not_13_out, BUS_IN[10]);
  not not_14 (not_14_out, BUS_IN[11]);
  and and_1 (and_1_out, not_1_out, Load);
  and and_2 (and_2_out, not_1_out, not_2_out, Incriment);
  and and_3 (and_3_out, and_1_out, BUS_IN[0]);
  and and_4 (and_4_out, and_1_out, not_3_out);
  and and_5 (and_5_out, and_1_out, BUS_IN[1]);
  and and_6 (and_6_out, and_1_out, not_4_out);
  and and_7 (and_7_out, and_1_out, BUS_IN[2]);
  and and_8 (and_8_out, and_1_out, not_5_out);
  and and_9 (and_9_out, and_1_out, BUS_IN[3]);
  and and_10 (and_10_out, and_1_out, not_6_out);
  and and_11 (and_11_out, and_1_out, BUS_IN[4]);
  and and_12 (and_12_out, and_1_out, not_7_out);
  and and_13 (and_13_out, and_1_out, BUS_IN[5]);
  and and_14 (and_14_out, and_1_out, not_8_out);
  and and_15 (and_15_out, and_1_out, BUS_IN[6]);
  and and_16 (and_16_out, and_1_out, not_9_out);
  and and_17 (and_17_out, and_1_out, BUS_IN[7]);
  and and_18 (and_18_out, and_1_out, not_10_out);
  and and_19 (and_19_out, and_1_out, BUS_IN[8]);
  and and_20 (and_20_out, and_1_out, not_11_out);
  and and_21 (and_21_out, and_1_out, BUS_IN[9]);
  and and_22 (and_22_out, and_1_out, not_12_out);
  and and_23 (and_23_out, and_1_out, BUS_IN[10]);
  and and_24 (and_24_out, and_1_out, not_13_out);
  and and_25 (and_25_out, and_1_out, BUS_IN[11]);
  and and_26 (and_26_out, and_1_out, not_14_out);
  and and_27 (and_27_out, and_2_out, BUS_OUT[0]);
  and and_28 (and_28_out, and_27_out, BUS_OUT[1]);
  and and_29 (and_29_out, and_28_out, BUS_OUT[2]);
  and and_30 (and_30_out, and_29_out, BUS_OUT[3]);
  and and_31 (and_31_out, and_30_out, BUS_OUT[4]);
  and and_32 (and_32_out, and_31_out, BUS_OUT[5]);
  and and_33 (and_33_out, and_32_out, BUS_OUT[6]);
  and and_34 (and_34_out, and_33_out, BUS_OUT[7]);
  and and_35 (and_35_out, and_34_out, BUS_OUT[8]);
  and and_36 (and_36_out, and_35_out, BUS_OUT[9]);
  and and_37 (and_37_out, and_36_out, BUS_OUT[10]);
  or or_1 (or_1_out, and_2_out, and_3_out);
  or or_2 (or_2_out, Clear, and_2_out, and_4_out);
  or or_3 (or_3_out, and_27_out, and_5_out);
  or or_4 (or_4_out, Clear, and_27_out, and_6_out);
  or or_5 (or_5_out, and_28_out, and_7_out);
  or or_6 (or_6_out, Clear, and_28_out, and_8_out);
  or or_7 (or_7_out, and_29_out, and_9_out);
  or or_8 (or_8_out, Clear, and_29_out, and_10_out);
  or or_9 (or_9_out, and_30_out, and_11_out);
  or or_10 (or_10_out, Clear, and_30_out, and_12_out);
  or or_11 (or_11_out, and_31_out, and_13_out);
  or or_12 (or_12_out, Clear, and_31_out, and_14_out);
  or or_13 (or_13_out, and_32_out, and_15_out);
  or or_14 (or_14_out, Clear, and_32_out, and_16_out);
  or or_15 (or_15_out, and_33_out, and_17_out);
  or or_16 (or_16_out, Clear, and_33_out, and_18_out);
  or or_17 (or_17_out, and_34_out, and_19_out);
  or or_18 (or_18_out, Clear, and_34_out, and_20_out);
  or or_19 (or_19_out, and_35_out, and_21_out);
  or or_20 (or_20_out, Clear, and_35_out, and_22_out);
  or or_21 (or_21_out, and_36_out, and_23_out);
  or or_22 (or_22_out, Clear, and_36_out, and_24_out);
  or or_23 (or_23_out, and_37_out, and_25_out);
  or or_24 (or_24_out, Clear, and_37_out, and_26_out);
  J_K_Flip_Flop j_k_ff_1 (.J(or_1_out), .clk(Clock), .K(or_2_out), .Q(BUS_OUT[0]));  // open: Qn, preset, en, reset
  J_K_Flip_Flop j_k_ff_2 (.J(or_3_out), .clk(Clock), .K(or_4_out), .Q(BUS_OUT[1]));  // open: Qn, preset, en, reset
  J_K_Flip_Flop j_k_ff_3 (.J(or_5_out), .clk(Clock), .K(or_6_out), .Q(BUS_OUT[2]));  // open: Qn, preset, en, reset
  J_K_Flip_Flop j_k_ff_4 (.J(or_7_out), .clk(Clock), .K(or_8_out), .Q(BUS_OUT[3]));  // open: Qn, preset, en, reset
  J_K_Flip_Flop j_k_ff_5 (.J(or_9_out), .clk(Clock), .K(or_10_out), .Q(BUS_OUT[4]));  // open: Qn, preset, en, reset
  J_K_Flip_Flop j_k_ff_6 (.J(or_11_out), .clk(Clock), .K(or_12_out), .Q(BUS_OUT[5]));  // open: Qn, preset, en, reset
  J_K_Flip_Flop j_k_ff_7 (.J(or_13_out), .clk(Clock), .K(or_14_out), .Q(BUS_OUT[6]));  // open: Qn, preset, en, reset
  J_K_Flip_Flop j_k_ff_8 (.J(or_15_out), .clk(Clock), .K(or_16_out), .Q(BUS_OUT[7]));  // open: Qn, preset, en, reset
  J_K_Flip_Flop j_k_ff_9 (.J(or_17_out), .clk(Clock), .K(or_18_out), .Q(BUS_OUT[8]));  // open: Qn, preset, en, reset
  J_K_Flip_Flop j_k_ff_10 (.J(or_19_out), .clk(Clock), .K(or_20_out), .Q(BUS_OUT[9]));  // open: Qn, preset, en, reset
  J_K_Flip_Flop j_k_ff_11 (.J(or_21_out), .clk(Clock), .K(or_22_out), .Q(BUS_OUT[10]));  // open: Qn, preset, en, reset
  J_K_Flip_Flop j_k_ff_12 (.J(or_23_out), .clk(Clock), .K(or_24_out), .Q(BUS_OUT[11]));  // open: Qn, preset, en, reset
  and and_38 (and_38_out, BUS_OUT[11], and_37_out);

  // Notes on the sheet:
  //   ADDRESS REGISTER
  //   Carry
  //   Bu Proje Sakarya Uygulamalı Bilimler Üniversitesi 
  //   Bilgisayar Mühendisliği Öğrencisi Furkan Duran Tarafından Yapılmıştır.
  //   İletişime geçmek için b210109048@subu.edu.tr mail adresini kullanabilirsiniz
endmodule

module AR_Controller (
  input  [15:0] IR,
  input  [2:0] T,
  input  R,
  output Load,
  output Clear,
  output Increment
);

  wire and_1_out, and_2_out, and_3_out, decoder_1_out0, decoder_1_out2, decoder_1_out3, decoder_1_out4,
       decoder_2_out5, decoder_2_out7;

  Decoder #(.select(3), .enable("false")) decoder_1 (
    .out0(decoder_1_out0), .out2(decoder_1_out2), .out3(decoder_1_out3), .out4(decoder_1_out4), .sel(T));  // open: out1, out5, out6, out7
  Decoder #(.select(3), .enable("false")) decoder_2 (
    .out5(decoder_2_out5), .out7(decoder_2_out7), .sel(IR[14:12]));  // open: out0, out1, out2, out3, out4, out6
  and and_1 (and_1_out, ~R, decoder_1_out0);  // AND_Gate
  and and_2 (and_2_out, ~decoder_2_out7, IR[15], decoder_1_out3);  // AND_Gate
  and and_3 (and_3_out, ~R, decoder_1_out2);  // AND_Gate
  and and_4 (Clear, R, decoder_1_out0);
  and and_5 (Increment, decoder_2_out5, decoder_1_out4);
  or or_1 (Load, and_1_out, and_2_out, and_3_out);

  // Notes on the sheet:
  //   T0R'
  //   D7'IT3
  //   T2R'
  //   T0R
  //   D5T4
  //   Load için gelen AND kapıları
  //   ------------------------------------
  //   1.AND =  R'T0         AR <- PC
  //   Bu Proje Sakarya Uygulamalı Bilimler Üniversitesi 
  //   2.AND =   D7'IT3  indirect    AR <- M[AR]
  //   3.AND =  R'T2       decode 2.aşama     AR <- IR(0-11)
  //   Clear için gelen AND kapıları
  //   ------------------------------------
  //   1.AND =  RT0  AR<- 0
  //   Arttırma için gelen AND kapsı
  //   ------------------------------------
  //   1.AND =  D5T4  AR <- AR + 1
  //   Bilgisayar Mühendisliği Öğrencisi Furkan Duran Tarafından Yapılmıştır.
  //   İletişime geçmek için b210109048@subu.edu.tr mail adresini kullanabilirsiniz
endmodule

module PC (
  input  Clear,
  input  Load,
  input  Incriment,
  input  [11:0] BUS_IN,
  input  Clock,
  output [11:0] BUS_OUT
);

  wire and_1_out, and_2_out, and_3_out, and_4_out, and_5_out, and_6_out, and_7_out, and_8_out, and_9_out,
       and_10_out, and_11_out, and_12_out, and_13_out, and_14_out, and_15_out, and_16_out, and_17_out,
       and_18_out, and_19_out, and_20_out, and_21_out, and_22_out, and_23_out, and_24_out, and_25_out,
       and_26_out, and_27_out, and_28_out, and_29_out, and_30_out, and_31_out, and_32_out, and_33_out,
       and_34_out, and_35_out, and_36_out, and_37_out, and_38_out, not_1_out, not_2_out, not_3_out,
       not_4_out, not_5_out, not_6_out, not_7_out, not_8_out, not_9_out, not_10_out, not_11_out, not_12_out,
       not_13_out, not_14_out, or_1_out, or_2_out, or_3_out, or_4_out, or_5_out, or_6_out, or_7_out,
       or_8_out, or_9_out, or_10_out, or_11_out, or_12_out, or_13_out, or_14_out, or_15_out, or_16_out,
       or_17_out, or_18_out, or_19_out, or_20_out, or_21_out, or_22_out, or_23_out, or_24_out;

  not not_1 (not_1_out, Clear);
  not not_2 (not_2_out, Load);
  not not_3 (not_3_out, BUS_IN[0]);
  not not_4 (not_4_out, BUS_IN[1]);
  not not_5 (not_5_out, BUS_IN[2]);
  not not_6 (not_6_out, BUS_IN[3]);
  not not_7 (not_7_out, BUS_IN[4]);
  not not_8 (not_8_out, BUS_IN[5]);
  not not_9 (not_9_out, BUS_IN[6]);
  not not_10 (not_10_out, BUS_IN[7]);
  not not_11 (not_11_out, BUS_IN[8]);
  not not_12 (not_12_out, BUS_IN[9]);
  not not_13 (not_13_out, BUS_IN[10]);
  not not_14 (not_14_out, BUS_IN[11]);
  and and_1 (and_1_out, not_1_out, Load);
  and and_2 (and_2_out, not_1_out, not_2_out, Incriment);
  and and_3 (and_3_out, and_1_out, BUS_IN[0]);
  and and_4 (and_4_out, and_1_out, not_3_out);
  and and_5 (and_5_out, and_1_out, BUS_IN[1]);
  and and_6 (and_6_out, and_1_out, not_4_out);
  and and_7 (and_7_out, and_1_out, BUS_IN[2]);
  and and_8 (and_8_out, and_1_out, not_5_out);
  and and_9 (and_9_out, and_1_out, BUS_IN[3]);
  and and_10 (and_10_out, and_1_out, not_6_out);
  and and_11 (and_11_out, and_1_out, BUS_IN[4]);
  and and_12 (and_12_out, and_1_out, not_7_out);
  and and_13 (and_13_out, and_1_out, BUS_IN[5]);
  and and_14 (and_14_out, and_1_out, not_8_out);
  and and_15 (and_15_out, and_1_out, BUS_IN[6]);
  and and_16 (and_16_out, and_1_out, not_9_out);
  and and_17 (and_17_out, and_1_out, BUS_IN[7]);
  and and_18 (and_18_out, and_1_out, not_10_out);
  and and_19 (and_19_out, and_1_out, BUS_IN[8]);
  and and_20 (and_20_out, and_1_out, not_11_out);
  and and_21 (and_21_out, and_1_out, BUS_IN[9]);
  and and_22 (and_22_out, and_1_out, not_12_out);
  and and_23 (and_23_out, and_1_out, BUS_IN[10]);
  and and_24 (and_24_out, and_1_out, not_13_out);
  and and_25 (and_25_out, and_1_out, BUS_IN[11]);
  and and_26 (and_26_out, and_1_out, not_14_out);
  and and_27 (and_27_out, and_2_out, BUS_OUT[0]);
  and and_28 (and_28_out, and_27_out, BUS_OUT[1]);
  and and_29 (and_29_out, and_28_out, BUS_OUT[2]);
  and and_30 (and_30_out, and_29_out, BUS_OUT[3]);
  and and_31 (and_31_out, and_30_out, BUS_OUT[4]);
  and and_32 (and_32_out, and_31_out, BUS_OUT[5]);
  and and_33 (and_33_out, and_32_out, BUS_OUT[6]);
  and and_34 (and_34_out, and_33_out, BUS_OUT[7]);
  and and_35 (and_35_out, and_34_out, BUS_OUT[8]);
  and and_36 (and_36_out, and_35_out, BUS_OUT[9]);
  and and_37 (and_37_out, and_36_out, BUS_OUT[10]);
  or or_1 (or_1_out, and_2_out, and_3_out);
  or or_2 (or_2_out, Clear, and_2_out, and_4_out);
  or or_3 (or_3_out, and_27_out, and_5_out);
  or or_4 (or_4_out, Clear, and_27_out, and_6_out);
  or or_5 (or_5_out, and_28_out, and_7_out);
  or or_6 (or_6_out, Clear, and_28_out, and_8_out);
  or or_7 (or_7_out, and_29_out, and_9_out);
  or or_8 (or_8_out, Clear, and_29_out, and_10_out);
  or or_9 (or_9_out, and_30_out, and_11_out);
  or or_10 (or_10_out, Clear, and_30_out, and_12_out);
  or or_11 (or_11_out, and_31_out, and_13_out);
  or or_12 (or_12_out, Clear, and_31_out, and_14_out);
  or or_13 (or_13_out, and_32_out, and_15_out);
  or or_14 (or_14_out, Clear, and_32_out, and_16_out);
  or or_15 (or_15_out, and_33_out, and_17_out);
  or or_16 (or_16_out, Clear, and_33_out, and_18_out);
  or or_17 (or_17_out, and_34_out, and_19_out);
  or or_18 (or_18_out, Clear, and_34_out, and_20_out);
  or or_19 (or_19_out, and_35_out, and_21_out);
  or or_20 (or_20_out, Clear, and_35_out, and_22_out);
  or or_21 (or_21_out, and_36_out, and_23_out);
  or or_22 (or_22_out, Clear, and_36_out, and_24_out);
  or or_23 (or_23_out, and_37_out, and_25_out);
  or or_24 (or_24_out, Clear, and_37_out, and_26_out);
  J_K_Flip_Flop j_k_ff_1 (.J(or_1_out), .clk(Clock), .K(or_2_out), .Q(BUS_OUT[0]));  // open: Qn, preset, en, reset
  J_K_Flip_Flop j_k_ff_2 (.J(or_3_out), .clk(Clock), .K(or_4_out), .Q(BUS_OUT[1]));  // open: Qn, preset, en, reset
  J_K_Flip_Flop j_k_ff_3 (.J(or_5_out), .clk(Clock), .K(or_6_out), .Q(BUS_OUT[2]));  // open: Qn, preset, en, reset
  J_K_Flip_Flop j_k_ff_4 (.J(or_7_out), .clk(Clock), .K(or_8_out), .Q(BUS_OUT[3]));  // open: Qn, preset, en, reset
  J_K_Flip_Flop j_k_ff_5 (.J(or_9_out), .clk(Clock), .K(or_10_out), .Q(BUS_OUT[4]));  // open: Qn, preset, en, reset
  J_K_Flip_Flop j_k_ff_6 (.J(or_11_out), .clk(Clock), .K(or_12_out), .Q(BUS_OUT[5]));  // open: Qn, preset, en, reset
  J_K_Flip_Flop j_k_ff_7 (.J(or_13_out), .clk(Clock), .K(or_14_out), .Q(BUS_OUT[6]));  // open: Qn, preset, en, reset
  J_K_Flip_Flop j_k_ff_8 (.J(or_15_out), .clk(Clock), .K(or_16_out), .Q(BUS_OUT[7]));  // open: Qn, preset, en, reset
  J_K_Flip_Flop j_k_ff_9 (.J(or_17_out), .clk(Clock), .K(or_18_out), .Q(BUS_OUT[8]));  // open: Qn, preset, en, reset
  J_K_Flip_Flop j_k_ff_10 (.J(or_19_out), .clk(Clock), .K(or_20_out), .Q(BUS_OUT[9]));  // open: Qn, preset, en, reset
  J_K_Flip_Flop j_k_ff_11 (.J(or_21_out), .clk(Clock), .K(or_22_out), .Q(BUS_OUT[10]));  // open: Qn, preset, en, reset
  J_K_Flip_Flop j_k_ff_12 (.J(or_23_out), .clk(Clock), .K(or_24_out), .Q(BUS_OUT[11]));  // open: Qn, preset, en, reset
  and and_38 (and_38_out, BUS_OUT[11], and_37_out);

  // Notes on the sheet:
  //   PROGRAM COUNTER
  //   Carry
  //   Bu Proje Sakarya Uygulamalı Bilimler Üniversitesi 
  //   Bilgisayar Mühendisliği Öğrencisi Furkan Duran Tarafından Yapılmıştır.
  //   İletişime geçmek için b210109048@subu.edu.tr mail adresini kullanabilirsiniz
endmodule

module PC_Controller (
  input  R,
  input  [15:0] IR,
  input  [15:0] DR,
  input  [15:0] AC,
  input  [2:0] T,
  input  FGI,
  input  FGO,
  input  E,
  output Load,
  output Increment,
  output Clear
);

  wire and_3_out, and_4_out, and_5_out, and_6_out, and_7_out, and_8_out, and_9_out, and_10_out, and_11_out,
       and_12_out, and_13_out, decoder_1_out1, decoder_1_out2, decoder_1_out3, decoder_1_out4,
       decoder_1_out5, decoder_1_out6, decoder_2_out4, decoder_2_out5, decoder_2_out6, decoder_2_out7,
       not_1_out, not_2_out, or_2_out, or_4_out, p, r_t;

  Decoder #(.select(3), .enable("false")) decoder_1 (
    .out1(decoder_1_out1), .out2(decoder_1_out2), .out3(decoder_1_out3), .out4(decoder_1_out4),
    .out5(decoder_1_out5), .out6(decoder_1_out6), .sel(T));  // open: out0, out7
  Decoder #(.select(3), .enable("false")) decoder_2 (
    .out4(decoder_2_out4), .out5(decoder_2_out5), .out6(decoder_2_out6), .out7(decoder_2_out7),
    .sel(IR[14:12]));  // open: out0, out1, out2, out3
  and and_1 (p, decoder_2_out7, IR[15], decoder_1_out3);
  and and_2 (r_t, decoder_2_out7, ~IR[15], decoder_1_out3);  // AND_Gate
  not not_1 (not_1_out, or_2_out);
  and and_3 (and_3_out, decoder_2_out4, decoder_1_out4);
  or or_1 (Load, and_3_out, and_4_out);
  and and_4 (and_4_out, decoder_2_out5, decoder_1_out5);
  and and_5 (and_5_out, ~R, decoder_1_out1);  // AND_Gate
  and and_6 (and_6_out, R, decoder_1_out2);
  and and_7 (and_7_out, decoder_1_out6, decoder_2_out6, not_1_out);
  and and_8 (and_8_out, ~AC[15], IR[4], r_t);  // AND_Gate
  and and_9 (and_9_out, AC[15], IR[3], r_t);
  and and_10 (and_10_out, not_2_out, IR[2], r_t);
  and and_11 (and_11_out, ~E, IR[1], r_t);  // AND_Gate
  and and_12 (and_12_out, IR[9], FGI, p);
  and and_13 (and_13_out, IR[8], FGO, p);
  and and_14 (Clear, R, decoder_1_out1);
  or or_2 (or_2_out, DR[15], DR[14], DR[13], DR[12], DR[11], DR[10], DR[9], DR[8], DR[7], DR[6], DR[5], DR[4], DR[3], DR[2], DR[1], DR[0]);
  not not_2 (not_2_out, or_4_out);
  or or_3 (Increment, and_5_out, and_6_out, and_7_out, and_8_out, and_9_out, and_10_out, and_11_out, and_12_out, and_13_out);
  or or_4 (or_4_out, AC[15], AC[14], AC[13], AC[12], AC[11], AC[10], AC[9], AC[8], AC[7], AC[6], AC[5], AC[4], AC[3], AC[2], AC[1], AC[0]);

  // Notes on the sheet:
  //   D7IT3
  //   D7I'T3
  //   IR(i)=Bi(6,...,11)
  //   Load için gelen AND kapıları
  //   ------------------------------------
  //   1.AND =  D4T4   PC<-AR
  //   2.AND =  D5T5   PC<-AR
  //   Clear için gelen AND kapıları
  //   ------------------------------------
  //   1.AND =  RT1  PC<- 0
  //   Arttırma için gelen AND kapıları
  //   ------------------------------------
  //   1.AND =  R'T1  PC<-PC + 1
  //   2.AND = RT2     PC<- PC + 1
  //   Bu Proje Sakarya Uygulamalı Bilimler Üniversitesi 
  //   3.AND = if (DR=0)   D6T6     PC<- PC + 1
  //   4.AND =if(AC(15)=0)   rB4      PC<- PC + 1  ---->   SPA
  //   5.AND =if(AC(15)=1)   rB4      PC<- PC + 1  ---->   SNA
  //   6.AND =if(AC=0)   rB2      PC<- PC + 1  ---->   SZA
  //   7.AND =if(E=0)   rB1      PC<- PC + 1  ---->   SNA
  //   8.AND =if(FGI=1)   pB9      PC<- PC + 1  ---->   SKI
  //   9.AND =if(FGO=1)   pB8      PC<- PC + 1  ---->   SKO
  //   Bilgisayar Mühendisliği Öğrencisi Furkan Duran Tarafından Yapılmıştır.
  //   İletişime geçmek için b210109048@subu.edu.tr mail adresini kullanabilirsiniz
  //   --------------
  //   2.GRUP
  //   --------------
  //   --------------
  //   3.GRUP
  //   --------------
endmodule

module DR (
  input  Clear,
  input  Load,
  input  Incriment,
  input  [15:0] BUS_IN,
  input  Clock,
  output [15:0] BUS_OUT
);

  wire and_1_out, and_2_out, and_3_out, and_4_out, and_5_out, and_6_out, and_7_out, and_8_out, and_9_out,
       and_10_out, and_11_out, and_12_out, and_13_out, and_14_out, and_15_out, and_16_out, and_17_out,
       and_18_out, and_19_out, and_20_out, and_21_out, and_22_out, and_23_out, and_24_out, and_25_out,
       and_26_out, and_27_out, and_28_out, and_29_out, and_30_out, and_31_out, and_32_out, and_33_out,
       and_34_out, and_35_out, and_36_out, and_37_out, and_38_out, and_39_out, and_40_out, and_41_out,
       and_42_out, and_43_out, and_44_out, and_45_out, and_46_out, and_47_out, and_48_out, and_49_out,
       and_50_out, not_1_out, not_2_out, not_3_out, not_4_out, not_5_out, not_6_out, not_7_out, not_8_out,
       not_9_out, not_10_out, not_11_out, not_12_out, not_13_out, not_14_out, not_15_out, not_16_out,
       not_17_out, not_18_out, or_1_out, or_2_out, or_3_out, or_4_out, or_5_out, or_6_out, or_7_out,
       or_8_out, or_9_out, or_10_out, or_11_out, or_12_out, or_13_out, or_14_out, or_15_out, or_16_out,
       or_17_out, or_18_out, or_19_out, or_20_out, or_21_out, or_22_out, or_23_out, or_24_out, or_25_out,
       or_26_out, or_27_out, or_28_out, or_29_out, or_30_out, or_31_out, or_32_out;

  not not_1 (not_1_out, BUS_IN[0]);
  not not_2 (not_2_out, BUS_IN[1]);
  not not_3 (not_3_out, BUS_IN[2]);
  not not_4 (not_4_out, BUS_IN[3]);
  not not_5 (not_5_out, BUS_IN[4]);
  not not_6 (not_6_out, BUS_IN[5]);
  not not_7 (not_7_out, BUS_IN[6]);
  not not_8 (not_8_out, BUS_IN[7]);
  not not_9 (not_9_out, BUS_IN[8]);
  not not_10 (not_10_out, BUS_IN[9]);
  not not_11 (not_11_out, BUS_IN[10]);
  not not_12 (not_12_out, BUS_IN[11]);
  not not_13 (not_13_out, BUS_IN[12]);
  not not_14 (not_14_out, BUS_IN[13]);
  not not_15 (not_15_out, BUS_IN[14]);
  not not_16 (not_16_out, BUS_IN[15]);
  not not_17 (not_17_out, Clear);
  not not_18 (not_18_out, Load);
  and and_1 (and_1_out, not_17_out, Load);
  and and_2 (and_2_out, not_17_out, not_18_out, Incriment);
  and and_3 (and_3_out, and_1_out, BUS_IN[0]);
  and and_4 (and_4_out, and_1_out, not_1_out);
  and and_5 (and_5_out, and_2_out, BUS_OUT[0]);
  and and_6 (and_6_out, and_1_out, BUS_IN[1]);
  and and_7 (and_7_out, and_1_out, not_2_out);
  and and_8 (and_8_out, and_1_out, BUS_IN[2]);
  and and_9 (and_9_out, and_1_out, not_3_out);
  and and_10 (and_10_out, and_1_out, BUS_IN[3]);
  and and_11 (and_11_out, and_1_out, not_4_out);
  and and_12 (and_12_out, and_1_out, BUS_IN[4]);
  and and_13 (and_13_out, and_1_out, not_5_out);
  and and_14 (and_14_out, and_1_out, BUS_IN[5]);
  and and_15 (and_15_out, and_1_out, not_6_out);
  and and_16 (and_16_out, and_1_out, BUS_IN[6]);
  and and_17 (and_17_out, and_1_out, not_7_out);
  and and_18 (and_18_out, and_1_out, BUS_IN[7]);
  and and_19 (and_19_out, and_1_out, not_8_out);
  and and_20 (and_20_out, and_1_out, BUS_IN[8]);
  and and_21 (and_21_out, and_1_out, not_9_out);
  and and_22 (and_22_out, and_1_out, BUS_IN[9]);
  and and_23 (and_23_out, and_1_out, not_10_out);
  and and_24 (and_24_out, and_1_out, BUS_IN[10]);
  and and_25 (and_25_out, and_1_out, not_11_out);
  and and_26 (and_26_out, and_1_out, BUS_IN[11]);
  and and_27 (and_27_out, and_1_out, not_12_out);
  and and_28 (and_28_out, and_1_out, BUS_IN[12]);
  and and_29 (and_29_out, and_1_out, not_13_out);
  and and_30 (and_30_out, and_1_out, BUS_IN[13]);
  and and_31 (and_31_out, and_1_out, not_14_out);
  and and_32 (and_32_out, and_1_out, BUS_IN[14]);
  and and_33 (and_33_out, and_1_out, not_15_out);
  and and_34 (and_34_out, and_1_out, BUS_IN[15]);
  and and_35 (and_35_out, and_1_out, not_16_out);
  and and_36 (and_36_out, and_5_out, BUS_OUT[1]);
  and and_37 (and_37_out, and_36_out, BUS_OUT[2]);
  and and_38 (and_38_out, and_37_out, BUS_OUT[3]);
  and and_39 (and_39_out, and_38_out, BUS_OUT[4]);
  and and_40 (and_40_out, and_39_out, BUS_OUT[5]);
  and and_41 (and_41_out, and_40_out, BUS_OUT[6]);
  and and_42 (and_42_out, and_41_out, BUS_OUT[7]);
  and and_43 (and_43_out, and_42_out, BUS_OUT[8]);
  and and_44 (and_44_out, and_43_out, BUS_OUT[9]);
  and and_45 (and_45_out, and_44_out, BUS_OUT[10]);
  and and_46 (and_46_out, and_45_out, BUS_OUT[11]);
  and and_47 (and_47_out, and_46_out, BUS_OUT[12]);
  and and_48 (and_48_out, and_47_out, BUS_OUT[13]);
  and and_49 (and_49_out, and_48_out, BUS_OUT[14]);
  or or_1 (or_1_out, and_2_out, and_3_out);
  or or_2 (or_2_out, Clear, and_2_out, and_4_out);
  or or_3 (or_3_out, and_5_out, and_6_out);
  or or_4 (or_4_out, Clear, and_5_out, and_7_out);
  or or_5 (or_5_out, and_36_out, and_8_out);
  or or_6 (or_6_out, Clear, and_36_out, and_9_out);
  or or_7 (or_7_out, and_37_out, and_10_out);
  or or_8 (or_8_out, Clear, and_37_out, and_11_out);
  or or_9 (or_9_out, and_38_out, and_12_out);
  or or_10 (or_10_out, Clear, and_38_out, and_13_out);
  or or_11 (or_11_out, and_39_out, and_14_out);
  or or_12 (or_12_out, Clear, and_39_out, and_15_out);
  or or_13 (or_13_out, and_40_out, and_16_out);
  or or_14 (or_14_out, Clear, and_40_out, and_17_out);
  or or_15 (or_15_out, and_41_out, and_18_out);
  or or_16 (or_16_out, Clear, and_41_out, and_19_out);
  or or_17 (or_17_out, and_42_out, and_20_out);
  or or_18 (or_18_out, Clear, and_42_out, and_21_out);
  or or_19 (or_19_out, and_43_out, and_22_out);
  or or_20 (or_20_out, Clear, and_43_out, and_23_out);
  or or_21 (or_21_out, and_44_out, and_24_out);
  or or_22 (or_22_out, Clear, and_44_out, and_25_out);
  or or_23 (or_23_out, and_45_out, and_26_out);
  or or_24 (or_24_out, Clear, and_45_out, and_27_out);
  or or_25 (or_25_out, and_46_out, and_28_out);
  or or_26 (or_26_out, Clear, and_46_out, and_29_out);
  or or_27 (or_27_out, and_47_out, and_30_out);
  or or_28 (or_28_out, Clear, and_47_out, and_31_out);
  or or_29 (or_29_out, and_48_out, and_32_out);
  or or_30 (or_30_out, Clear, and_48_out, and_33_out);
  or or_31 (or_31_out, and_49_out, and_34_out);
  or or_32 (or_32_out, Clear, and_49_out, and_35_out);
  J_K_Flip_Flop j_k_ff_1 (.J(or_1_out), .clk(Clock), .K(or_2_out), .Q(BUS_OUT[0]));  // open: Qn, preset, en, reset
  J_K_Flip_Flop j_k_ff_2 (.J(or_3_out), .clk(Clock), .K(or_4_out), .Q(BUS_OUT[1]));  // open: Qn, preset, en, reset
  J_K_Flip_Flop j_k_ff_3 (.J(or_5_out), .clk(Clock), .K(or_6_out), .Q(BUS_OUT[2]));  // open: Qn, preset, en, reset
  J_K_Flip_Flop j_k_ff_4 (.J(or_7_out), .clk(Clock), .K(or_8_out), .Q(BUS_OUT[3]));  // open: Qn, preset, en, reset
  J_K_Flip_Flop j_k_ff_5 (.J(or_9_out), .clk(Clock), .K(or_10_out), .Q(BUS_OUT[4]));  // open: Qn, preset, en, reset
  J_K_Flip_Flop j_k_ff_6 (.J(or_31_out), .clk(Clock), .K(or_32_out), .Q(BUS_OUT[15]));  // open: Qn, preset, en, reset
  and and_50 (and_50_out, BUS_OUT[15], and_49_out);
  J_K_Flip_Flop j_k_ff_7 (.J(or_11_out), .clk(Clock), .K(or_12_out), .Q(BUS_OUT[5]));  // open: Qn, preset, en, reset
  J_K_Flip_Flop j_k_ff_8 (.J(or_13_out), .clk(Clock), .K(or_14_out), .Q(BUS_OUT[6]));  // open: Qn, preset, en, reset
  J_K_Flip_Flop j_k_ff_9 (.J(or_15_out), .clk(Clock), .K(or_16_out), .Q(BUS_OUT[7]));  // open: Qn, preset, en, reset
  J_K_Flip_Flop j_k_ff_10 (.J(or_17_out), .clk(Clock), .K(or_18_out), .Q(BUS_OUT[8]));  // open: Qn, preset, en, reset
  J_K_Flip_Flop j_k_ff_11 (.J(or_19_out), .clk(Clock), .K(or_20_out), .Q(BUS_OUT[9]));  // open: Qn, preset, en, reset
  J_K_Flip_Flop j_k_ff_12 (.J(or_21_out), .clk(Clock), .K(or_22_out), .Q(BUS_OUT[10]));  // open: Qn, preset, en, reset
  J_K_Flip_Flop j_k_ff_13 (.J(or_23_out), .clk(Clock), .K(or_24_out), .Q(BUS_OUT[11]));  // open: Qn, preset, en, reset
  J_K_Flip_Flop j_k_ff_14 (.J(or_25_out), .clk(Clock), .K(or_26_out), .Q(BUS_OUT[12]));  // open: Qn, preset, en, reset
  J_K_Flip_Flop j_k_ff_15 (.J(or_27_out), .clk(Clock), .K(or_28_out), .Q(BUS_OUT[13]));  // open: Qn, preset, en, reset
  J_K_Flip_Flop j_k_ff_16 (.J(or_29_out), .clk(Clock), .K(or_30_out), .Q(BUS_OUT[14]));  // open: Qn, preset, en, reset

  // Notes on the sheet:
  //   DATA REGISTER
  //   Bu Proje Sakarya Uygulamalı Bilimler Üniversitesi 
  //   Bilgisayar Mühendisliği Öğrencisi Furkan Duran Tarafından Yapılmıştır.
  //   İletişime geçmek için b210109048@subu.edu.tr mail adresini kullanabilirsiniz
  //   Carry
endmodule

module DR_Controller (
  input  [2:0] T,
  input  [15:0] IR,
  output Load,
  output Increment
);

  wire decoder_1_out4, decoder_1_out5, decoder_2_out0, decoder_2_out1, decoder_2_out2, decoder_2_out6,
       or_1_out;

  Decoder #(.select(3), .enable("false")) decoder_1 (
    .out4(decoder_1_out4), .out5(decoder_1_out5), .sel(T));  // open: out0, out1, out2, out3, out6, out7
  Decoder #(.select(3), .enable("false")) decoder_2 (
    .out0(decoder_2_out0), .out1(decoder_2_out1), .out2(decoder_2_out2), .out6(decoder_2_out6),
    .sel(IR[14:12]));  // open: out3, out4, out5, out7
  and and_1 (Increment, decoder_2_out6, decoder_1_out5);
  or or_1 (or_1_out, decoder_2_out0, decoder_2_out1, decoder_2_out2, decoder_2_out6);
  and and_2 (Load, decoder_1_out4, or_1_out);

  // Notes on the sheet:
  //   Increment için gelen AND kapısı
  //   ------------------------------------
  //   D6T5          DR<- DR + 1 
  //   Load için gelen AND kapısı
  //   ------------------------------------
  //   D0T4 + D1T4 + D2T4 + D6T4
  //   Bu Proje Sakarya Uygulamalı Bilimler Üniversitesi 
  //   Bilgisayar Mühendisliği Öğrencisi Furkan Duran Tarafından Yapılmıştır.
  //   İletişime geçmek için b210109048@subu.edu.tr mail adresini kullanabilirsiniz
endmodule

module AC (
  input  Clear,
  input  Load,
  input  Incriment,
  input  [15:0] ALU_IN,
  input  Clock,
  output [15:0] BUS_OUT
);

  wire and_1_out, and_2_out, and_3_out, and_4_out, and_5_out, and_6_out, and_7_out, and_8_out, and_9_out,
       and_10_out, and_11_out, and_12_out, and_13_out, and_14_out, and_15_out, and_16_out, and_17_out,
       and_18_out, and_19_out, and_20_out, and_21_out, and_22_out, and_23_out, and_24_out, and_25_out,
       and_26_out, and_27_out, and_28_out, and_29_out, and_30_out, and_31_out, and_32_out, and_33_out,
       and_34_out, and_35_out, and_36_out, and_37_out, and_38_out, and_39_out, and_40_out, and_41_out,
       and_42_out, and_43_out, and_44_out, and_45_out, and_46_out, and_47_out, and_48_out, and_49_out,
       and_50_out, not_1_out, not_2_out, not_3_out, not_4_out, not_5_out, not_6_out, not_7_out, not_8_out,
       not_9_out, not_10_out, not_11_out, not_12_out, not_13_out, not_14_out, not_15_out, not_16_out,
       not_17_out, not_18_out, or_1_out, or_2_out, or_3_out, or_4_out, or_5_out, or_6_out, or_7_out,
       or_8_out, or_9_out, or_10_out, or_11_out, or_12_out, or_13_out, or_14_out, or_15_out, or_16_out,
       or_17_out, or_18_out, or_19_out, or_20_out, or_21_out, or_22_out, or_23_out, or_24_out, or_25_out,
       or_26_out, or_27_out, or_28_out, or_29_out, or_30_out, or_31_out, or_32_out;

  not not_1 (not_1_out, ALU_IN[0]);
  not not_2 (not_2_out, ALU_IN[1]);
  not not_3 (not_3_out, ALU_IN[2]);
  not not_4 (not_4_out, ALU_IN[3]);
  not not_5 (not_5_out, ALU_IN[4]);
  not not_6 (not_6_out, ALU_IN[5]);
  not not_7 (not_7_out, ALU_IN[6]);
  not not_8 (not_8_out, ALU_IN[7]);
  not not_9 (not_9_out, ALU_IN[8]);
  not not_10 (not_10_out, ALU_IN[9]);
  not not_11 (not_11_out, ALU_IN[10]);
  not not_12 (not_12_out, ALU_IN[11]);
  not not_13 (not_13_out, ALU_IN[12]);
  not not_14 (not_14_out, ALU_IN[13]);
  not not_15 (not_15_out, ALU_IN[14]);
  not not_16 (not_16_out, ALU_IN[15]);
  not not_17 (not_17_out, Clear);
  not not_18 (not_18_out, Load);
  and and_1 (and_1_out, not_17_out, Load);
  and and_2 (and_2_out, not_17_out, not_18_out, Incriment);
  and and_3 (and_3_out, and_1_out, ALU_IN[0]);
  and and_4 (and_4_out, and_1_out, not_1_out);
  and and_5 (and_5_out, and_2_out, BUS_OUT[0]);
  and and_6 (and_6_out, and_1_out, ALU_IN[1]);
  and and_7 (and_7_out, and_1_out, not_2_out);
  and and_8 (and_8_out, and_1_out, ALU_IN[2]);
  and and_9 (and_9_out, and_1_out, not_3_out);
  and and_10 (and_10_out, and_1_out, ALU_IN[3]);
  and and_11 (and_11_out, and_1_out, not_4_out);
  and and_12 (and_12_out, and_1_out, ALU_IN[4]);
  and and_13 (and_13_out, and_1_out, not_5_out);
  and and_14 (and_14_out, and_1_out, ALU_IN[5]);
  and and_15 (and_15_out, and_1_out, not_6_out);
  and and_16 (and_16_out, and_1_out, ALU_IN[6]);
  and and_17 (and_17_out, and_1_out, not_7_out);
  and and_18 (and_18_out, and_1_out, ALU_IN[7]);
  and and_19 (and_19_out, and_1_out, not_8_out);
  and and_20 (and_20_out, and_1_out, ALU_IN[8]);
  and and_21 (and_21_out, and_1_out, not_9_out);
  and and_22 (and_22_out, and_1_out, ALU_IN[9]);
  and and_23 (and_23_out, and_1_out, not_10_out);
  and and_24 (and_24_out, and_1_out, ALU_IN[10]);
  and and_25 (and_25_out, and_1_out, not_11_out);
  and and_26 (and_26_out, and_1_out, ALU_IN[11]);
  and and_27 (and_27_out, and_1_out, not_12_out);
  and and_28 (and_28_out, and_1_out, ALU_IN[12]);
  and and_29 (and_29_out, and_1_out, not_13_out);
  and and_30 (and_30_out, and_1_out, ALU_IN[13]);
  and and_31 (and_31_out, and_1_out, not_14_out);
  and and_32 (and_32_out, and_1_out, ALU_IN[14]);
  and and_33 (and_33_out, and_1_out, not_15_out);
  and and_34 (and_34_out, and_1_out, ALU_IN[15]);
  and and_35 (and_35_out, and_1_out, not_16_out);
  and and_36 (and_36_out, and_5_out, BUS_OUT[1]);
  and and_37 (and_37_out, and_36_out, BUS_OUT[2]);
  and and_38 (and_38_out, and_37_out, BUS_OUT[3]);
  and and_39 (and_39_out, and_38_out, BUS_OUT[4]);
  and and_40 (and_40_out, and_39_out, BUS_OUT[5]);
  and and_41 (and_41_out, and_40_out, BUS_OUT[6]);
  and and_42 (and_42_out, and_41_out, BUS_OUT[7]);
  and and_43 (and_43_out, and_42_out, BUS_OUT[8]);
  and and_44 (and_44_out, and_43_out, BUS_OUT[9]);
  and and_45 (and_45_out, and_44_out, BUS_OUT[10]);
  and and_46 (and_46_out, and_45_out, BUS_OUT[11]);
  and and_47 (and_47_out, and_46_out, BUS_OUT[12]);
  and and_48 (and_48_out, and_47_out, BUS_OUT[13]);
  and and_49 (and_49_out, and_48_out, BUS_OUT[14]);
  or or_1 (or_1_out, and_2_out, and_3_out);
  or or_2 (or_2_out, Clear, and_2_out, and_4_out);
  or or_3 (or_3_out, and_5_out, and_6_out);
  or or_4 (or_4_out, Clear, and_5_out, and_7_out);
  or or_5 (or_5_out, and_36_out, and_8_out);
  or or_6 (or_6_out, Clear, and_36_out, and_9_out);
  or or_7 (or_7_out, and_37_out, and_10_out);
  or or_8 (or_8_out, Clear, and_37_out, and_11_out);
  or or_9 (or_9_out, and_38_out, and_12_out);
  or or_10 (or_10_out, Clear, and_38_out, and_13_out);
  or or_11 (or_11_out, and_39_out, and_14_out);
  or or_12 (or_12_out, Clear, and_39_out, and_15_out);
  or or_13 (or_13_out, and_40_out, and_16_out);
  or or_14 (or_14_out, Clear, and_40_out, and_17_out);
  or or_15 (or_15_out, and_41_out, and_18_out);
  or or_16 (or_16_out, Clear, and_41_out, and_19_out);
  or or_17 (or_17_out, and_42_out, and_20_out);
  or or_18 (or_18_out, Clear, and_42_out, and_21_out);
  or or_19 (or_19_out, and_43_out, and_22_out);
  or or_20 (or_20_out, Clear, and_43_out, and_23_out);
  or or_21 (or_21_out, and_44_out, and_24_out);
  or or_22 (or_22_out, Clear, and_44_out, and_25_out);
  or or_23 (or_23_out, and_45_out, and_26_out);
  or or_24 (or_24_out, Clear, and_45_out, and_27_out);
  or or_25 (or_25_out, and_46_out, and_28_out);
  or or_26 (or_26_out, Clear, and_46_out, and_29_out);
  or or_27 (or_27_out, and_47_out, and_30_out);
  or or_28 (or_28_out, Clear, and_47_out, and_31_out);
  or or_29 (or_29_out, and_48_out, and_32_out);
  or or_30 (or_30_out, Clear, and_48_out, and_33_out);
  or or_31 (or_31_out, and_49_out, and_34_out);
  or or_32 (or_32_out, Clear, and_49_out, and_35_out);
  J_K_Flip_Flop j_k_ff_1 (.J(or_1_out), .clk(Clock), .K(or_2_out), .Q(BUS_OUT[0]));  // open: Qn, preset, en, reset
  J_K_Flip_Flop j_k_ff_2 (.J(or_3_out), .clk(Clock), .K(or_4_out), .Q(BUS_OUT[1]));  // open: Qn, preset, en, reset
  J_K_Flip_Flop j_k_ff_3 (.J(or_5_out), .clk(Clock), .K(or_6_out), .Q(BUS_OUT[2]));  // open: Qn, preset, en, reset
  J_K_Flip_Flop j_k_ff_4 (.J(or_7_out), .clk(Clock), .K(or_8_out), .Q(BUS_OUT[3]));  // open: Qn, preset, en, reset
  J_K_Flip_Flop j_k_ff_5 (.J(or_9_out), .clk(Clock), .K(or_10_out), .Q(BUS_OUT[4]));  // open: Qn, preset, en, reset
  J_K_Flip_Flop j_k_ff_6 (.J(or_31_out), .clk(Clock), .K(or_32_out), .Q(BUS_OUT[15]));  // open: Qn, preset, en, reset
  and and_50 (and_50_out, BUS_OUT[15], and_49_out);
  J_K_Flip_Flop j_k_ff_7 (.J(or_11_out), .clk(Clock), .K(or_12_out), .Q(BUS_OUT[5]));  // open: Qn, preset, en, reset
  J_K_Flip_Flop j_k_ff_8 (.J(or_13_out), .clk(Clock), .K(or_14_out), .Q(BUS_OUT[6]));  // open: Qn, preset, en, reset
  J_K_Flip_Flop j_k_ff_9 (.J(or_15_out), .clk(Clock), .K(or_16_out), .Q(BUS_OUT[7]));  // open: Qn, preset, en, reset
  J_K_Flip_Flop j_k_ff_10 (.J(or_17_out), .clk(Clock), .K(or_18_out), .Q(BUS_OUT[8]));  // open: Qn, preset, en, reset
  J_K_Flip_Flop j_k_ff_11 (.J(or_19_out), .clk(Clock), .K(or_20_out), .Q(BUS_OUT[9]));  // open: Qn, preset, en, reset
  J_K_Flip_Flop j_k_ff_12 (.J(or_21_out), .clk(Clock), .K(or_22_out), .Q(BUS_OUT[10]));  // open: Qn, preset, en, reset
  J_K_Flip_Flop j_k_ff_13 (.J(or_23_out), .clk(Clock), .K(or_24_out), .Q(BUS_OUT[11]));  // open: Qn, preset, en, reset
  J_K_Flip_Flop j_k_ff_14 (.J(or_25_out), .clk(Clock), .K(or_26_out), .Q(BUS_OUT[12]));  // open: Qn, preset, en, reset
  J_K_Flip_Flop j_k_ff_15 (.J(or_27_out), .clk(Clock), .K(or_28_out), .Q(BUS_OUT[13]));  // open: Qn, preset, en, reset
  J_K_Flip_Flop j_k_ff_16 (.J(or_29_out), .clk(Clock), .K(or_30_out), .Q(BUS_OUT[14]));  // open: Qn, preset, en, reset

  // Notes on the sheet:
  //   ACCUMULATOR
  //   Bu Proje Sakarya Uygulamalı Bilimler Üniversitesi 
  //   Bilgisayar Mühendisliği Öğrencisi Furkan Duran Tarafından Yapılmıştır.
  //   İletişime geçmek için b210109048@subu.edu.tr mail adresini kullanabilirsiniz
  //   Carry
endmodule

module AC_Controller (
  input  [15:0] IR,
  input  [2:0] T,
  output Clear,
  output Increment
);

  wire decoder_1_out3, decoder_2_out7, p, r;

  Decoder #(.select(3), .enable("false")) decoder_1 (
    .out3(decoder_1_out3), .sel(T));  // open: out0, out1, out2, out4, out5, out6, out7
  Decoder #(.select(3), .enable("false")) decoder_2 (
    .out7(decoder_2_out7), .sel(IR[14:12]));  // open: out0, out1, out2, out3, out4, out5, out6
  and and_1 (p, decoder_1_out3, IR[15], decoder_2_out7);
  and and_2 (r, decoder_1_out3, ~IR[15], decoder_2_out7);  // AND_Gate
  and and_3 (Clear, IR[11], r);
  and and_4 (Increment, IR[5], r);

  // Notes on the sheet:
  //   D7I'T3 
  //   D7IT3 
  //   IR(i)=Bi(0,...,11)
  //   Clear için gelen AND kapısı
  //   ------------------------------------
  //   rB(11)       AC <- 0 
  //   Increment için gelen AND kapısı
  //   ------------------------------------
  //   rB(5)       AC <- AC + 1 
  //   Bu Proje Sakarya Uygulamalı Bilimler Üniversitesi 
  //   Bilgisayar Mühendisliği Öğrencisi Furkan Duran Tarafından Yapılmıştır.
  //   İletişime geçmek için b210109048@subu.edu.tr mail adresini kullanabilirsiniz
endmodule

module IR (
  input  Clear,
  input  Load,
  input  Incriment,
  input  [15:0] BUS_IN,
  input  Clock,
  output [15:0] BUS_OUT
);

  wire and_1_out, and_2_out, and_3_out, and_4_out, and_5_out, and_6_out, and_7_out, and_8_out, and_9_out,
       and_10_out, and_11_out, and_12_out, and_13_out, and_14_out, and_15_out, and_16_out, and_17_out,
       and_18_out, and_19_out, and_20_out, and_21_out, and_22_out, and_23_out, and_24_out, and_25_out,
       and_26_out, and_27_out, and_28_out, and_29_out, and_30_out, and_31_out, and_32_out, and_33_out,
       and_34_out, and_35_out, and_36_out, and_37_out, and_38_out, and_39_out, and_40_out, and_41_out,
       and_42_out, and_43_out, and_44_out, and_45_out, and_46_out, and_47_out, and_48_out, and_49_out,
       and_50_out, and_51_out, and_52_out, and_53_out, and_54_out, and_55_out, and_56_out, and_57_out,
       and_58_out, not_1_out, not_2_out, not_3_out, not_4_out, not_5_out, not_6_out, not_7_out, not_8_out,
       not_9_out, not_10_out, not_11_out, not_12_out, not_13_out, not_14_out, not_15_out, not_16_out,
       not_17_out, not_18_out, not_19_out, not_20_out, not_21_out, or_1_out, or_2_out, or_3_out, or_4_out,
       or_5_out, or_6_out, or_7_out, or_8_out, or_9_out, or_10_out, or_11_out, or_12_out, or_13_out,
       or_14_out, or_15_out, or_16_out, or_17_out, or_18_out, or_19_out, or_20_out, or_21_out, or_22_out,
       or_23_out, or_24_out, or_25_out, or_26_out, or_27_out, or_28_out, or_29_out, or_30_out, or_31_out,
       or_32_out;

  not not_1 (not_1_out, BUS_IN[0]);
  not not_2 (not_2_out, BUS_IN[1]);
  not not_3 (not_3_out, BUS_IN[2]);
  not not_4 (not_4_out, BUS_IN[3]);
  not not_5 (not_5_out, BUS_IN[4]);
  not not_6 (not_6_out, BUS_IN[5]);
  not not_7 (not_7_out, BUS_IN[6]);
  not not_8 (not_8_out, BUS_IN[7]);
  not not_9 (not_9_out, BUS_IN[8]);
  not not_10 (not_10_out, BUS_IN[9]);
  not not_11 (not_11_out, BUS_IN[10]);
  not not_12 (not_12_out, BUS_IN[11]);
  not not_13 (not_13_out, BUS_IN[12]);
  not not_14 (not_14_out, BUS_IN[13]);
  not not_15 (not_15_out, BUS_IN[14]);
  not not_16 (not_16_out, BUS_IN[15]);
  not not_17 (not_17_out, Clear);
  not not_18 (not_18_out, Load);
  and and_1 (and_1_out, not_17_out, Load);
  and and_2 (and_2_out, not_17_out, not_18_out, Incriment);
  and and_3 (and_3_out, and_1_out, BUS_IN[0]);
  and and_4 (and_4_out, and_1_out, not_1_out);
  and and_5 (and_5_out, and_2_out, BUS_OUT[0]);
  and and_6 (and_6_out, and_1_out, BUS_IN[1]);
  and and_7 (and_7_out, and_1_out, not_2_out);
  and and_8 (and_8_out, and_1_out, BUS_IN[2]);
  and and_9 (and_9_out, and_1_out, not_3_out);
  and and_10 (and_10_out, and_1_out, BUS_IN[3]);
  and and_11 (and_11_out, and_1_out, not_4_out);
  and and_12 (and_12_out, and_1_out, BUS_IN[4]);
  and and_13 (and_13_out, and_1_out, not_5_out);
  and and_14 (and_14_out, and_1_out, BUS_IN[5]);
  and and_15 (and_15_out, and_1_out, not_6_out);
  and and_16 (and_16_out, and_1_out, BUS_IN[6]);
  and and_17 (and_17_out, and_1_out, not_7_out);
  and and_18 (and_18_out, and_1_out, BUS_IN[7]);
  and and_19 (and_19_out, and_1_out, not_8_out);
  and and_20 (and_20_out, and_1_out, BUS_IN[8]);
  and and_21 (and_21_out, and_1_out, not_9_out);
  and and_22 (and_22_out, and_1_out, BUS_IN[9]);
  and and_23 (and_23_out, and_1_out, not_10_out);
  and and_24 (and_24_out, and_1_out, BUS_IN[10]);
  and and_25 (and_25_out, and_1_out, not_11_out);
  and and_26 (and_26_out, and_1_out, BUS_IN[11]);
  and and_27 (and_27_out, and_1_out, not_12_out);
  and and_28 (and_28_out, and_1_out, BUS_IN[12]);
  and and_29 (and_29_out, and_1_out, not_13_out);
  and and_30 (and_30_out, and_1_out, BUS_IN[13]);
  and and_31 (and_31_out, and_1_out, not_14_out);
  and and_32 (and_32_out, and_1_out, BUS_IN[14]);
  and and_33 (and_33_out, and_1_out, not_15_out);
  and and_34 (and_34_out, and_1_out, BUS_IN[15]);
  and and_35 (and_35_out, and_1_out, not_16_out);
  and and_36 (and_36_out, and_5_out, BUS_OUT[1]);
  and and_37 (and_37_out, and_36_out, BUS_OUT[2]);
  and and_38 (and_38_out, and_37_out, BUS_OUT[3]);
  and and_39 (and_39_out, and_38_out, BUS_OUT[4]);
  and and_40 (and_40_out, and_39_out, BUS_OUT[5]);
  and and_41 (and_41_out, and_40_out, BUS_OUT[6]);
  and and_42 (and_42_out, and_41_out, BUS_OUT[7]);
  and and_43 (and_43_out, and_42_out, BUS_OUT[8]);
  and and_44 (and_44_out, and_43_out, BUS_OUT[9]);
  and and_45 (and_45_out, and_44_out, BUS_OUT[10]);
  and and_46 (and_46_out, and_45_out, BUS_OUT[11]);
  and and_47 (and_47_out, and_46_out, BUS_OUT[12]);
  and and_48 (and_48_out, and_47_out, BUS_OUT[13]);
  and and_49 (and_49_out, and_48_out, BUS_OUT[14]);
  or or_1 (or_1_out, and_2_out, and_3_out);
  or or_2 (or_2_out, Clear, and_2_out, and_4_out);
  or or_3 (or_3_out, and_5_out, and_6_out);
  or or_4 (or_4_out, Clear, and_5_out, and_7_out);
  or or_5 (or_5_out, and_36_out, and_8_out);
  or or_6 (or_6_out, Clear, and_36_out, and_9_out);
  or or_7 (or_7_out, and_37_out, and_10_out);
  or or_8 (or_8_out, Clear, and_37_out, and_11_out);
  or or_9 (or_9_out, and_38_out, and_12_out);
  or or_10 (or_10_out, Clear, and_38_out, and_13_out);
  or or_11 (or_11_out, and_39_out, and_14_out);
  or or_12 (or_12_out, Clear, and_39_out, and_15_out);
  or or_13 (or_13_out, and_40_out, and_16_out);
  or or_14 (or_14_out, Clear, and_40_out, and_17_out);
  or or_15 (or_15_out, and_41_out, and_18_out);
  or or_16 (or_16_out, Clear, and_41_out, and_19_out);
  or or_17 (or_17_out, and_42_out, and_20_out);
  or or_18 (or_18_out, Clear, and_42_out, and_21_out);
  or or_19 (or_19_out, and_43_out, and_22_out);
  or or_20 (or_20_out, Clear, and_43_out, and_23_out);
  or or_21 (or_21_out, and_44_out, and_24_out);
  or or_22 (or_22_out, Clear, and_44_out, and_25_out);
  or or_23 (or_23_out, and_45_out, and_26_out);
  or or_24 (or_24_out, Clear, and_45_out, and_27_out);
  or or_25 (or_25_out, and_46_out, and_28_out);
  or or_26 (or_26_out, Clear, and_46_out, and_29_out);
  or or_27 (or_27_out, and_47_out, and_30_out);
  or or_28 (or_28_out, Clear, and_47_out, and_31_out);
  or or_29 (or_29_out, and_48_out, and_32_out);
  or or_30 (or_30_out, Clear, and_48_out, and_33_out);
  or or_31 (or_31_out, and_49_out, and_34_out);
  or or_32 (or_32_out, Clear, and_49_out, and_35_out);
  J_K_Flip_Flop j_k_ff_1 (.J(or_1_out), .clk(Clock), .K(or_2_out), .Q(BUS_OUT[0]));  // open: Qn, preset, en, reset
  J_K_Flip_Flop j_k_ff_2 (.J(or_3_out), .clk(Clock), .K(or_4_out), .Q(BUS_OUT[1]));  // open: Qn, preset, en, reset
  J_K_Flip_Flop j_k_ff_3 (.J(or_5_out), .clk(Clock), .K(or_6_out), .Q(BUS_OUT[2]));  // open: Qn, preset, en, reset
  J_K_Flip_Flop j_k_ff_4 (.J(or_7_out), .clk(Clock), .K(or_8_out), .Q(BUS_OUT[3]));  // open: Qn, preset, en, reset
  J_K_Flip_Flop j_k_ff_5 (.J(or_9_out), .clk(Clock), .K(or_10_out), .Q(BUS_OUT[4]));  // open: Qn, preset, en, reset
  J_K_Flip_Flop j_k_ff_6 (.J(or_31_out), .clk(Clock), .K(or_32_out), .Q(BUS_OUT[15]));  // open: Qn, preset, en, reset
  and and_50 (and_50_out, BUS_OUT[15], and_49_out);
  J_K_Flip_Flop j_k_ff_7 (.J(or_11_out), .clk(Clock), .K(or_12_out), .Q(BUS_OUT[5]));  // open: Qn, preset, en, reset
  J_K_Flip_Flop j_k_ff_8 (.J(or_13_out), .clk(Clock), .K(or_14_out), .Q(BUS_OUT[6]));  // open: Qn, preset, en, reset
  J_K_Flip_Flop j_k_ff_9 (.J(or_15_out), .clk(Clock), .K(or_16_out), .Q(BUS_OUT[7]));  // open: Qn, preset, en, reset
  J_K_Flip_Flop j_k_ff_10 (.J(or_17_out), .clk(Clock), .K(or_18_out), .Q(BUS_OUT[8]));  // open: Qn, preset, en, reset
  J_K_Flip_Flop j_k_ff_11 (.J(or_19_out), .clk(Clock), .K(or_20_out), .Q(BUS_OUT[9]));  // open: Qn, preset, en, reset
  J_K_Flip_Flop j_k_ff_12 (.J(or_21_out), .clk(Clock), .K(or_22_out), .Q(BUS_OUT[10]));  // open: Qn, preset, en, reset
  J_K_Flip_Flop j_k_ff_13 (.J(or_23_out), .clk(Clock), .K(or_24_out), .Q(BUS_OUT[11]));  // open: Qn, preset, en, reset
  J_K_Flip_Flop j_k_ff_14 (.J(or_25_out), .clk(Clock), .K(or_26_out), .Q(BUS_OUT[12]));  // open: Qn, preset, en, reset
  J_K_Flip_Flop j_k_ff_15 (.J(or_27_out), .clk(Clock), .K(or_28_out), .Q(BUS_OUT[13]));  // open: Qn, preset, en, reset
  J_K_Flip_Flop j_k_ff_16 (.J(or_29_out), .clk(Clock), .K(or_30_out), .Q(BUS_OUT[14]));  // open: Qn, preset, en, reset
  not not_19 (not_19_out, BUS_OUT[14]);
  not not_20 (not_20_out, BUS_OUT[13]);
  not not_21 (not_21_out, BUS_OUT[12]);
  and and_51 (and_51_out, not_21_out, not_20_out, not_19_out);
  and and_52 (and_52_out, not_19_out, not_20_out, BUS_OUT[12]);
  and and_53 (and_53_out, not_19_out, BUS_OUT[13], not_21_out);
  and and_54 (and_54_out, not_19_out, BUS_OUT[13], BUS_OUT[12]);
  and and_55 (and_55_out, BUS_OUT[14], not_20_out, not_21_out);
  and and_56 (and_56_out, BUS_OUT[14], not_20_out, BUS_OUT[12]);
  and and_57 (and_57_out, BUS_OUT[14], BUS_OUT[13], not_21_out);
  and and_58 (and_58_out, BUS_OUT[14], BUS_OUT[13], BUS_OUT[12]);

  // Other names for the same wires on the sheet: IR_12 = BUS_OUT[12]; IR_13 = BUS_OUT[13]; IR_14 = BUS_OUT[14];
  //   I = BUS_OUT[15]

  // Notes on the sheet:
  //   INSTRUCTION REGISTER
  //   Bu Proje Sakarya Uygulamalı Bilimler Üniversitesi 
  //   Bilgisayar Mühendisliği Öğrencisi Furkan Duran Tarafından Yapılmıştır.
  //   İletişime geçmek için b210109048@subu.edu.tr mail adresini kullanabilirsiniz
  //   Carry
  //   D0
  //   D1
  //   D2
  //   D3
  //   D4
  //   D5
  //   D6
  //   D7
endmodule

module IR_Controller (
  input  [2:0] T,
  input  R,
  output Load
);

  wire decoder_1_out1;

  Decoder #(.select(3), .enable("false")) decoder_1 (
    .out1(decoder_1_out1), .sel(T));  // open: out0, out2, out3, out4, out5, out6, out7
  and and_1 (Load, ~R, decoder_1_out1);  // AND_Gate

  // Notes on the sheet:
  //   Load için gelen AND kapısı
  //   ------------------------------------
  //   R'T1        IR <- M[AR]
  //   Bu Proje Sakarya Uygulamalı Bilimler Üniversitesi 
  //   Bilgisayar Mühendisliği Öğrencisi Furkan Duran Tarafından Yapılmıştır.
  //   İletişime geçmek için b210109048@subu.edu.tr mail adresini kullanabilirsiniz
endmodule

module TR (
  input  Clear,
  input  Load,
  input  Incriment,
  input  [15:0] BUS_IN,
  input  Clock,
  output [15:0] BUS_OUT
);

  wire and_1_out, and_2_out, and_3_out, and_4_out, and_5_out, and_6_out, and_7_out, and_8_out, and_9_out,
       and_10_out, and_11_out, and_12_out, and_13_out, and_14_out, and_15_out, and_16_out, and_17_out,
       and_18_out, and_19_out, and_20_out, and_21_out, and_22_out, and_23_out, and_24_out, and_25_out,
       and_26_out, and_27_out, and_28_out, and_29_out, and_30_out, and_31_out, and_32_out, and_33_out,
       and_34_out, and_35_out, and_36_out, and_37_out, and_38_out, and_39_out, and_40_out, and_41_out,
       and_42_out, and_43_out, and_44_out, and_45_out, and_46_out, and_47_out, and_48_out, and_49_out,
       and_50_out, not_1_out, not_2_out, not_3_out, not_4_out, not_5_out, not_6_out, not_7_out, not_8_out,
       not_9_out, not_10_out, not_11_out, not_12_out, not_13_out, not_14_out, not_15_out, not_16_out,
       not_17_out, not_18_out, or_1_out, or_2_out, or_3_out, or_4_out, or_5_out, or_6_out, or_7_out,
       or_8_out, or_9_out, or_10_out, or_11_out, or_12_out, or_13_out, or_14_out, or_15_out, or_16_out,
       or_17_out, or_18_out, or_19_out, or_20_out, or_21_out, or_22_out, or_23_out, or_24_out, or_25_out,
       or_26_out, or_27_out, or_28_out, or_29_out, or_30_out, or_31_out, or_32_out;

  not not_1 (not_1_out, Clear);
  not not_2 (not_2_out, Load);
  not not_3 (not_3_out, BUS_IN[0]);
  not not_4 (not_4_out, BUS_IN[1]);
  not not_5 (not_5_out, BUS_IN[2]);
  not not_6 (not_6_out, BUS_IN[3]);
  not not_7 (not_7_out, BUS_IN[4]);
  not not_8 (not_8_out, BUS_IN[5]);
  not not_9 (not_9_out, BUS_IN[6]);
  not not_10 (not_10_out, BUS_IN[7]);
  not not_11 (not_11_out, BUS_IN[8]);
  not not_12 (not_12_out, BUS_IN[9]);
  not not_13 (not_13_out, BUS_IN[10]);
  not not_14 (not_14_out, BUS_IN[11]);
  not not_15 (not_15_out, BUS_IN[12]);
  not not_16 (not_16_out, BUS_IN[13]);
  not not_17 (not_17_out, BUS_IN[14]);
  not not_18 (not_18_out, BUS_IN[15]);
  and and_1 (and_1_out, not_1_out, Load);
  and and_2 (and_2_out, not_1_out, not_2_out, Incriment);
  and and_3 (and_3_out, and_1_out, BUS_IN[0]);
  and and_4 (and_4_out, and_1_out, not_3_out);
  and and_5 (and_5_out, and_1_out, BUS_IN[1]);
  and and_6 (and_6_out, and_1_out, not_4_out);
  and and_7 (and_7_out, and_1_out, BUS_IN[2]);
  and and_8 (and_8_out, and_1_out, not_5_out);
  and and_9 (and_9_out, and_1_out, BUS_IN[3]);
  and and_10 (and_10_out, and_1_out, not_6_out);
  and and_11 (and_11_out, and_1_out, BUS_IN[4]);
  and and_12 (and_12_out, and_1_out, not_7_out);
  and and_13 (and_13_out, and_1_out, BUS_IN[5]);
  and and_14 (and_14_out, and_1_out, not_8_out);
  and and_15 (and_15_out, and_1_out, BUS_IN[6]);
  and and_16 (and_16_out, and_1_out, not_9_out);
  and and_17 (and_17_out, and_1_out, BUS_IN[7]);
  and and_18 (and_18_out, and_1_out, not_10_out);
  and and_19 (and_19_out, and_1_out, BUS_IN[8]);
  and and_20 (and_20_out, and_1_out, not_11_out);
  and and_21 (and_21_out, and_1_out, BUS_IN[9]);
  and and_22 (and_22_out, and_1_out, not_12_out);
  and and_23 (and_23_out, and_1_out, BUS_IN[10]);
  and and_24 (and_24_out, and_1_out, not_13_out);
  and and_25 (and_25_out, and_1_out, BUS_IN[11]);
  and and_26 (and_26_out, and_1_out, not_14_out);
  and and_27 (and_27_out, and_1_out, BUS_IN[12]);
  and and_28 (and_28_out, and_1_out, not_15_out);
  and and_29 (and_29_out, and_1_out, BUS_IN[13]);
  and and_30 (and_30_out, and_1_out, not_16_out);
  and and_31 (and_31_out, and_1_out, BUS_IN[14]);
  and and_32 (and_32_out, and_1_out, not_17_out);
  and and_33 (and_33_out, and_1_out, BUS_IN[15]);
  and and_34 (and_34_out, and_1_out, not_18_out);
  and and_35 (and_35_out, and_2_out, BUS_OUT[0]);
  and and_36 (and_36_out, and_35_out, BUS_OUT[1]);
  and and_37 (and_37_out, and_36_out, BUS_OUT[2]);
  and and_38 (and_38_out, and_37_out, BUS_OUT[3]);
  and and_39 (and_39_out, and_38_out, BUS_OUT[4]);
  and and_40 (and_40_out, and_39_out, BUS_OUT[5]);
  and and_41 (and_41_out, and_40_out, BUS_OUT[6]);
  and and_42 (and_42_out, and_41_out, BUS_OUT[7]);
  and and_43 (and_43_out, and_42_out, BUS_OUT[8]);
  and and_44 (and_44_out, and_43_out, BUS_OUT[9]);
  and and_45 (and_45_out, and_44_out, BUS_OUT[10]);
  and and_46 (and_46_out, and_45_out, BUS_OUT[11]);
  and and_47 (and_47_out, and_46_out, BUS_OUT[12]);
  and and_48 (and_48_out, and_47_out, BUS_OUT[13]);
  and and_49 (and_49_out, and_48_out, BUS_OUT[14]);
  or or_1 (or_1_out, and_2_out, and_3_out);
  or or_2 (or_2_out, Clear, and_2_out, and_4_out);
  or or_3 (or_3_out, and_35_out, and_5_out);
  or or_4 (or_4_out, Clear, and_35_out, and_6_out);
  or or_5 (or_5_out, and_36_out, and_7_out);
  or or_6 (or_6_out, Clear, and_36_out, and_8_out);
  or or_7 (or_7_out, and_37_out, and_9_out);
  or or_8 (or_8_out, Clear, and_37_out, and_10_out);
  or or_9 (or_9_out, and_38_out, and_11_out);
  or or_10 (or_10_out, Clear, and_38_out, and_12_out);
  or or_11 (or_11_out, and_39_out, and_13_out);
  or or_12 (or_12_out, Clear, and_39_out, and_14_out);
  or or_13 (or_13_out, and_40_out, and_15_out);
  or or_14 (or_14_out, Clear, and_40_out, and_16_out);
  or or_15 (or_15_out, and_41_out, and_17_out);
  or or_16 (or_16_out, Clear, and_41_out, and_18_out);
  or or_17 (or_17_out, and_42_out, and_19_out);
  or or_18 (or_18_out, Clear, and_42_out, and_20_out);
  or or_19 (or_19_out, and_43_out, and_21_out);
  or or_20 (or_20_out, Clear, and_43_out, and_22_out);
  or or_21 (or_21_out, and_44_out, and_23_out);
  or or_22 (or_22_out, Clear, and_44_out, and_24_out);
  or or_23 (or_23_out, and_45_out, and_25_out);
  or or_24 (or_24_out, Clear, and_45_out, and_26_out);
  or or_25 (or_25_out, and_46_out, and_27_out);
  or or_26 (or_26_out, Clear, and_46_out, and_28_out);
  or or_27 (or_27_out, and_47_out, and_29_out);
  or or_28 (or_28_out, Clear, and_47_out, and_30_out);
  or or_29 (or_29_out, and_48_out, and_31_out);
  or or_30 (or_30_out, Clear, and_48_out, and_32_out);
  or or_31 (or_31_out, and_49_out, and_33_out);
  or or_32 (or_32_out, Clear, and_49_out, and_34_out);
  J_K_Flip_Flop j_k_ff_1 (.J(or_1_out), .clk(Clock), .K(or_2_out), .Q(BUS_OUT[0]));  // open: Qn, preset, en, reset
  J_K_Flip_Flop j_k_ff_2 (.J(or_3_out), .clk(Clock), .K(or_4_out), .Q(BUS_OUT[1]));  // open: Qn, preset, en, reset
  J_K_Flip_Flop j_k_ff_3 (.J(or_5_out), .clk(Clock), .K(or_6_out), .Q(BUS_OUT[2]));  // open: Qn, preset, en, reset
  J_K_Flip_Flop j_k_ff_4 (.J(or_7_out), .clk(Clock), .K(or_8_out), .Q(BUS_OUT[3]));  // open: Qn, preset, en, reset
  J_K_Flip_Flop j_k_ff_5 (.J(or_9_out), .clk(Clock), .K(or_10_out), .Q(BUS_OUT[4]));  // open: Qn, preset, en, reset
  J_K_Flip_Flop j_k_ff_6 (.J(or_11_out), .clk(Clock), .K(or_12_out), .Q(BUS_OUT[5]));  // open: Qn, preset, en, reset
  J_K_Flip_Flop j_k_ff_7 (.J(or_13_out), .clk(Clock), .K(or_14_out), .Q(BUS_OUT[6]));  // open: Qn, preset, en, reset
  J_K_Flip_Flop j_k_ff_8 (.J(or_15_out), .clk(Clock), .K(or_16_out), .Q(BUS_OUT[7]));  // open: Qn, preset, en, reset
  J_K_Flip_Flop j_k_ff_9 (.J(or_17_out), .clk(Clock), .K(or_18_out), .Q(BUS_OUT[8]));  // open: Qn, preset, en, reset
  J_K_Flip_Flop j_k_ff_10 (.J(or_19_out), .clk(Clock), .K(or_20_out), .Q(BUS_OUT[9]));  // open: Qn, preset, en, reset
  J_K_Flip_Flop j_k_ff_11 (.J(or_21_out), .clk(Clock), .K(or_22_out), .Q(BUS_OUT[10]));  // open: Qn, preset, en, reset
  J_K_Flip_Flop j_k_ff_12 (.J(or_23_out), .clk(Clock), .K(or_24_out), .Q(BUS_OUT[11]));  // open: Qn, preset, en, reset
  J_K_Flip_Flop j_k_ff_13 (.J(or_25_out), .clk(Clock), .K(or_26_out), .Q(BUS_OUT[12]));  // open: Qn, preset, en, reset
  J_K_Flip_Flop j_k_ff_14 (.J(or_27_out), .clk(Clock), .K(or_28_out), .Q(BUS_OUT[13]));  // open: Qn, preset, en, reset
  J_K_Flip_Flop j_k_ff_15 (.J(or_29_out), .clk(Clock), .K(or_30_out), .Q(BUS_OUT[14]));  // open: Qn, preset, en, reset
  J_K_Flip_Flop j_k_ff_16 (.J(or_31_out), .clk(Clock), .K(or_32_out), .Q(BUS_OUT[15]));  // open: Qn, preset, en, reset
  and and_50 (and_50_out, BUS_OUT[15], and_49_out);

  // Notes on the sheet:
  //   TEMPORARY REGISTER
  //   Bu Proje Sakarya Uygulamalı Bilimler Üniversitesi 
  //   Bilgisayar Mühendisliği Öğrencisi Furkan Duran Tarafından Yapılmıştır.
  //   İletişime geçmek için b210109048@subu.edu.tr mail adresini kullanabilirsiniz
  //   Carry
endmodule

module TR_Controller (
  input  [2:0] T,
  input  R,
  output Load
);

  wire decoder_1_out0;

  Decoder #(.select(3), .enable("false")) decoder_1 (
    .out0(decoder_1_out0), .sel(T));  // open: out1, out2, out3, out4, out5, out6, out7
  and and_1 (Load, R, decoder_1_out0);

  // Notes on the sheet:
  //   Load için gelen AND kapısı
  //   ------------------------------------
  //   RT0     TR <- PC
  //   Bu Proje Sakarya Uygulamalı Bilimler Üniversitesi 
  //   Bilgisayar Mühendisliği Öğrencisi Furkan Duran Tarafından Yapılmıştır.
  //   İletişime geçmek için b210109048@subu.edu.tr mail adresini kullanabilirsiniz
endmodule

module E (
  input  E_IN,
  input  Comp,
  input  Clock,
  input  load,
  input  Clear,
  output E_OUT
);

  wire and_1_out, multiplexer_1_out;

  Multiplexer #(.enable("false")) multiplexer_1 (.in0(E_IN), .in1(Comp), .out(multiplexer_1_out), .sel(Comp));
  and and_1 (and_1_out, multiplexer_1_out, Comp);
  J_K_Flip_Flop j_k_ff_1 (
    .J(multiplexer_1_out), .clk(Clock), .K(and_1_out), .Q(E_OUT), .en(load), .reset(Clear));  // open: Qn, preset

  // Notes on the sheet:
  //   Bu Proje Sakarya Uygulamalı Bilimler Üniversitesi 
  //   Bilgisayar Mühendisliği Öğrencisi Furkan Duran Tarafından Yapılmıştır.
  //   İletişime geçmek için b210109048@subu.edu.tr mail adresini kullanabilirsiniz
endmodule

module E_Controller (
  input  [15:0] IR,
  input  [2:0] T,
  output Comp,
  output Clear,
  output Load
);

  wire and_5_out, and_6_out, and_7_out, decoder_1_out3, decoder_1_out5, decoder_2_out1, decoder_2_out7, p, r;

  Decoder #(.select(3), .enable("false")) decoder_1 (
    .out3(decoder_1_out3), .out5(decoder_1_out5), .sel(T));  // open: out0, out1, out2, out4, out6, out7
  Decoder #(.select(3), .enable("false")) decoder_2 (
    .out1(decoder_2_out1), .out7(decoder_2_out7), .sel(IR[14:12]));  // open: out0, out2, out3, out4, out5, out6
  and and_1 (p, decoder_1_out3, IR[15], decoder_2_out7);
  and and_2 (r, decoder_1_out3, ~IR[15], decoder_2_out7);  // AND_Gate
  and and_3 (Comp, IR[8], r);
  and and_4 (Clear, IR[10], r);
  and and_5 (and_5_out, decoder_2_out1, decoder_1_out5);
  and and_6 (and_6_out, IR[7], r);
  and and_7 (and_7_out, IR[6], r);
  or or_1 (Load, and_5_out, and_6_out, and_7_out);

  // Notes on the sheet:
  //   IR(i)=Bi(0,...,11)
  //   Tümleyen için gelen AND kapısı
  //   ------------------------------------
  //   rB(8)     E <- E'
  //   Clear için gelen AND kapıları
  //   ------------------------------------
  //   rB(10)     E <- 0
  //   Load için gelen AND kapıları
  //   ------------------------------------
  //   D1T5       E <- Cout
  //   rB(7)   E <- AC(0)
  //   rB(6)   E <- AC(15)
  //   Bu Proje Sakarya Uygulamalı Bilimler Üniversitesi 
  //   Bilgisayar Mühendisliği Öğrencisi Furkan Duran Tarafından Yapılmıştır.
  //   İletişime geçmek için b210109048@subu.edu.tr mail adresini kullanabilirsiniz
endmodule

module OUTR (
  input  Clear,
  input  Load,
  input  Clk,
  input  Increment,
  input  [7:0] OUT_in,
  output [7:0] OUT
);

  wire and_1_out, and_2_out, and_3_out, and_4_out, and_5_out, and_6_out, and_7_out, and_8_out, and_9_out,
       and_10_out, and_11_out, and_12_out, and_13_out, and_14_out, and_15_out, and_16_out, and_17_out,
       and_18_out, and_19_out, and_20_out, and_21_out, and_22_out, and_23_out, and_24_out, and_25_out,
       not_1_out, not_2_out, not_3_out, not_4_out, not_5_out, not_6_out, not_7_out, not_8_out, not_9_out,
       not_10_out, or_1_out, or_2_out, or_3_out, or_4_out, or_5_out, or_6_out, or_7_out, or_8_out, or_9_out,
       or_10_out, or_11_out, or_12_out, or_13_out, or_14_out, or_15_out, or_16_out;

  not not_1 (not_1_out, Clear);
  and and_1 (and_1_out, not_1_out, Load);
  not not_2 (not_2_out, Load);
  and and_2 (and_2_out, not_1_out, not_2_out, Increment);
  not not_3 (not_3_out, OUT_in[0]);
  not not_4 (not_4_out, OUT_in[1]);
  not not_5 (not_5_out, OUT_in[2]);
  not not_6 (not_6_out, OUT_in[3]);
  not not_7 (not_7_out, OUT_in[4]);
  not not_8 (not_8_out, OUT_in[5]);
  not not_9 (not_9_out, OUT_in[6]);
  not not_10 (not_10_out, OUT_in[7]);
  and and_3 (and_3_out, and_1_out, OUT_in[0]);
  and and_4 (and_4_out, and_1_out, not_3_out);
  and and_5 (and_5_out, and_1_out, OUT_in[1]);
  and and_6 (and_6_out, and_1_out, not_4_out);
  and and_7 (and_7_out, and_1_out, OUT_in[2]);
  and and_8 (and_8_out, and_1_out, not_5_out);
  and and_9 (and_9_out, and_1_out, OUT_in[3]);
  and and_10 (and_10_out, and_1_out, not_6_out);
  and and_11 (and_11_out, and_1_out, OUT_in[4]);
  and and_12 (and_12_out, and_1_out, not_7_out);
  and and_13 (and_13_out, and_1_out, OUT_in[5]);
  and and_14 (and_14_out, and_1_out, not_8_out);
  and and_15 (and_15_out, and_1_out, OUT_in[6]);
  and and_16 (and_16_out, and_1_out, not_9_out);
  and and_17 (and_17_out, and_1_out, OUT_in[7]);
  and and_18 (and_18_out, and_1_out, not_10_out);
  or or_1 (or_1_out, and_2_out, and_3_out);
  or or_2 (or_2_out, Clear, and_2_out, and_4_out);
  and and_19 (and_19_out, and_2_out, OUT[0]);
  or or_3 (or_3_out, and_19_out, and_5_out);
  or or_4 (or_4_out, Clear, and_19_out, and_6_out);
  and and_20 (and_20_out, and_19_out, OUT[1]);
  or or_5 (or_5_out, and_20_out, and_7_out);
  or or_6 (or_6_out, Clear, and_20_out, and_8_out);
  and and_21 (and_21_out, and_20_out, OUT[2]);
  or or_7 (or_7_out, and_21_out, and_9_out);
  or or_8 (or_8_out, Clear, and_21_out, and_10_out);
  and and_22 (and_22_out, and_21_out, OUT[3]);
  or or_9 (or_9_out, and_22_out, and_11_out);
  or or_10 (or_10_out, Clear, and_22_out, and_12_out);
  and and_23 (and_23_out, and_22_out, OUT[4]);
  or or_11 (or_11_out, and_23_out, and_13_out);
  or or_12 (or_12_out, Clear, and_23_out, and_14_out);
  and and_24 (and_24_out, and_23_out, OUT[5]);
  or or_13 (or_13_out, and_24_out, and_15_out);
  or or_14 (or_14_out, Clear, and_24_out, and_16_out);
  and and_25 (and_25_out, and_24_out, OUT[6]);
  or or_15 (or_15_out, and_25_out, and_17_out);
  or or_16 (or_16_out, Clear, and_25_out, and_18_out);
  // AND_Gate and_26 has open pins: in0=and_25_out, in1=OUT[7], out=open
  J_K_Flip_Flop j_k_ff_1 (.J(or_1_out), .clk(Clk), .K(or_2_out), .Q(OUT[0]));  // open: Qn, preset, en, reset
  J_K_Flip_Flop j_k_ff_2 (.J(or_3_out), .clk(Clk), .K(or_4_out), .Q(OUT[1]));  // open: Qn, preset, en, reset
  J_K_Flip_Flop j_k_ff_3 (.J(or_5_out), .clk(Clk), .K(or_6_out), .Q(OUT[2]));  // open: Qn, preset, en, reset
  J_K_Flip_Flop j_k_ff_4 (.J(or_7_out), .clk(Clk), .K(or_8_out), .Q(OUT[3]));  // open: Qn, preset, en, reset
  J_K_Flip_Flop j_k_ff_5 (.J(or_9_out), .clk(Clk), .K(or_10_out), .Q(OUT[4]));  // open: Qn, preset, en, reset
  J_K_Flip_Flop j_k_ff_6 (.J(or_11_out), .clk(Clk), .K(or_12_out), .Q(OUT[5]));  // open: Qn, preset, en, reset
  J_K_Flip_Flop j_k_ff_7 (.J(or_13_out), .clk(Clk), .K(or_14_out), .Q(OUT[6]));  // open: Qn, preset, en, reset
  J_K_Flip_Flop j_k_ff_8 (.J(or_15_out), .clk(Clk), .K(or_16_out), .Q(OUT[7]));  // open: Qn, preset, en, reset

  // Notes on the sheet:
  //   Bu Proje Sakarya Uygulamalı Bilimler Üniversitesi 
  //   Bilgisayar Mühendisliği Öğrencisi Furkan Duran Tarafından Yapılmıştır.
  //   İletişime geçmek için b210109048@subu.edu.tr mail adresini kullanabilirsiniz
endmodule

module OUT_Controller (
  input  [15:0] IR,
  input  [2:0] T,
  output LD
);

  wire decoder_1_out3, decoder_2_out7, p;

  Decoder #(.select(3), .enable("false")) decoder_1 (
    .out3(decoder_1_out3), .sel(T));  // open: out0, out1, out2, out4, out5, out6, out7
  Decoder #(.select(3), .enable("false")) decoder_2 (
    .out7(decoder_2_out7), .sel(IR[14:12]));  // open: out0, out1, out2, out3, out4, out5, out6
  and and_1 (p, decoder_1_out3, IR[15], decoder_2_out7);
  and and_2 (LD, IR[10], p);

  // Notes on the sheet:
  //   Load için gelen AND kapıları
  //   ------------------------------------
  //   pB10   OUTR <- AC(0-7)
  //   Bu Proje Sakarya Uygulamalı Bilimler Üniversitesi 
  //   Bilgisayar Mühendisliği Öğrencisi Furkan Duran Tarafından Yapılmıştır.
  //   İletişime geçmek için b210109048@subu.edu.tr mail adresini kullanabilirsiniz
endmodule

module RAM_Controller (
  input  [15:0] IR,
  input  [2:0] T,
  input  R,
  output Load
);

  wire and_1_out, and_2_out, and_3_out, and_4_out, decoder_1_out1, decoder_1_out4, decoder_1_out6,
       decoder_2_out3, decoder_2_out5, decoder_2_out6, or_1_out;

  Decoder #(.select(3), .enable("false")) decoder_1 (
    .out1(decoder_1_out1), .out4(decoder_1_out4), .out6(decoder_1_out6), .sel(T));  // open: out0, out2, out3, out5, out7
  Decoder #(.select(3), .enable("false")) decoder_2 (
    .out3(decoder_2_out3), .out5(decoder_2_out5), .out6(decoder_2_out6), .sel(IR[14:12]));  // open: out0, out1, out2, out4, out7
  and and_1 (and_1_out, R, decoder_1_out1);
  and and_2 (and_2_out, decoder_2_out3, decoder_1_out4);
  and and_3 (and_3_out, decoder_2_out5, decoder_1_out4);
  and and_4 (and_4_out, decoder_2_out6, decoder_1_out6);
  or or_1 (or_1_out, and_1_out, and_2_out, and_3_out, and_4_out);
  not not_1 (Load, or_1_out);

  // Notes on the sheet:
  //   Load için gelen AND kapıları
  //   ------------------------------------
  //   RT1       M[AR] <- TR
  //   D3T4       M[AR] <- AC
  //   D5T4       M[AR] <- PC
  //   Bu Proje Sakarya Uygulamalı Bilimler Üniversitesi 
  //   Bilgisayar Mühendisliği Öğrencisi Furkan Duran Tarafından Yapılmıştır.
  //   İletişime geçmek için b210109048@subu.edu.tr mail adresini kullanabilirsiniz
  //   OUTR
endmodule

module SC (
  input  Clock,
  input  CLR,
  output out_3,
  output out_4,
  output out_5
);

  wire j_k_ff_1_qn, j_k_ff_2_qn, j_k_ff_3_qn;

  J_K_Flip_Flop j_k_ff_1 (
    .J(1'b1), .clk(Clock), .K(1'b1), .Q(out_5), .Qn(j_k_ff_1_qn), .reset(CLR));  // open: preset, en
  J_K_Flip_Flop j_k_ff_2 (
    .J(1'b1), .clk(j_k_ff_1_qn), .K(1'b1), .Q(out_4), .Qn(j_k_ff_2_qn), .reset(CLR));  // open: preset, en
  J_K_Flip_Flop j_k_ff_3 (
    .J(1'b1), .clk(j_k_ff_2_qn), .K(1'b1), .Q(out_3), .Qn(j_k_ff_3_qn), .reset(CLR));  // open: preset, en

  // Notes on the sheet:
  //   Bu Proje Sakarya Uygulamalı Bilimler Üniversitesi 
  //   Bilgisayar Mühendisliği Öğrencisi Furkan Duran Tarafından Yapılmıştır.
  //   İletişime geçmek için b210109048@subu.edu.tr mail adresini kullanabilirsiniz
endmodule

module SC_Controller (
  input  [15:0] IR,
  input  [2:0] T,
  input  R,
  output Clear
);

  wire and_3_out, and_4_out, and_5_out, and_6_out, and_7_out, and_8_out, and_9_out, and_10_out,
       decoder_1_out2, decoder_1_out3, decoder_1_out4, decoder_1_out5, decoder_1_out6, decoder_2_out0,
       decoder_2_out1, decoder_2_out2, decoder_2_out3, decoder_2_out4, decoder_2_out5, decoder_2_out6,
       decoder_2_out7, p, r_t;

  Decoder #(.select(3), .enable("false")) decoder_1 (
    .out2(decoder_1_out2), .out3(decoder_1_out3), .out4(decoder_1_out4), .out5(decoder_1_out5),
    .out6(decoder_1_out6), .sel(T));  // open: out0, out1, out7
  Decoder #(.select(3), .enable("false")) decoder_2 (
    .out0(decoder_2_out0), .out1(decoder_2_out1), .out2(decoder_2_out2), .out3(decoder_2_out3),
    .out4(decoder_2_out4), .out5(decoder_2_out5), .out6(decoder_2_out6), .out7(decoder_2_out7),
    .sel(IR[14:12]));
  and and_1 (p, decoder_1_out3, IR[15], decoder_2_out7);
  and and_2 (r_t, decoder_1_out3, ~IR[15], decoder_2_out7);  // AND_Gate
  and and_3 (and_3_out, decoder_1_out2, R);
  and and_4 (and_4_out, decoder_2_out0, decoder_1_out5);
  and and_5 (and_5_out, decoder_2_out1, decoder_1_out5);
  and and_6 (and_6_out, decoder_2_out2, decoder_1_out5);
  and and_7 (and_7_out, decoder_2_out3, decoder_1_out4);
  and and_8 (and_8_out, decoder_2_out4, decoder_1_out4);
  and and_9 (and_9_out, decoder_2_out5, decoder_1_out5);
  and and_10 (and_10_out, decoder_2_out6, decoder_1_out6);
  or or_1 (Clear, and_3_out, and_4_out, and_5_out, and_6_out, and_7_out, and_8_out, and_9_out, and_10_out, p, r_t);

  // Notes on the sheet:
  //   D7I'T3 
  //   D7IT3 
  //   Bu Proje Sakarya Uygulamalı Bilimler Üniversitesi 
  //   SC nin Sıfırlandığı Yerler
  //   ------------------------------------
  //   RT2       SC <- 0
  //   Bilgisayar Mühendisliği Öğrencisi Furkan Duran Tarafından Yapılmıştır.
  //   İletişime geçmek için b210109048@subu.edu.tr mail adresini kullanabilirsiniz
endmodule

module R_Controller (
  input  [2:0] T,
  input  IEN,
  input  FGO,
  input  FGI,
  output R
);

  wire and_1_out, and_2_out, and_3_out, decoder_1_out0, decoder_1_out1, decoder_1_out2, or_1_out;

  Decoder #(.select(3), .enable("false")) decoder_1 (
    .out0(decoder_1_out0), .out1(decoder_1_out1), .out2(decoder_1_out2), .sel(T));  // open: out3, out4, out5, out6, out7
  or or_1 (or_1_out, FGO, FGI);
  and and_1 (and_1_out, ~decoder_1_out0, ~decoder_1_out1, ~decoder_1_out2);  // AND_Gate
  and and_2 (and_2_out, IEN, and_1_out, or_1_out);
  and and_3 (and_3_out, decoder_1_out2, R);
  J_K_Flip_Flop j_k_ff_1 (.J(and_2_out), .clk(T[0]), .K(and_3_out), .Q(R));  // open: Qn, preset, en, reset

  // Notes on the sheet:
  //   T0'T1'T2'
  //   T0'T1'T2'(IEN)(FGI + FGO)
  //   RT2
  //   Bu Proje Sakarya Uygulamalı Bilimler Üniversitesi 
  //   Bilgisayar Mühendisliği Öğrencisi Furkan Duran Tarafından Yapılmıştır.
  //   İletişime geçmek için b210109048@subu.edu.tr mail adresini kullanabilirsiniz
endmodule

module FGI (
  input  FGI_J,
  input  FGI_K,
  input  Clock,
  output FGI
);

  J_K_Flip_Flop j_k_ff_1 (.J(FGI_J), .clk(Clock), .K(FGI_K), .Q(FGI));  // open: Qn, preset, en, reset

  // Notes on the sheet:
  //   Bu Proje Sakarya Uygulamalı Bilimler Üniversitesi 
  //   Bilgisayar Mühendisliği Öğrencisi Furkan Duran Tarafından Yapılmıştır.
  //   İletişime geçmek için b210109048@subu.edu.tr mail adresini kullanabilirsiniz
endmodule

module FGO (
  input  FGO_J,
  input  FGO_K,
  input  Clock,
  output FGO
);

  J_K_Flip_Flop j_k_ff_1 (.J(FGO_J), .clk(Clock), .K(FGO_K), .Q(FGO));  // open: Qn, preset, en, reset

  // Notes on the sheet:
  //   Bu Proje Sakarya Uygulamalı Bilimler Üniversitesi 
  //   Bilgisayar Mühendisliği Öğrencisi Furkan Duran Tarafından Yapılmıştır.
  //   İletişime geçmek için b210109048@subu.edu.tr mail adresini kullanabilirsiniz
endmodule

module IEN (
  input  IEN_J,
  input  Clock,
  input  IEN_K,
  output IEN
);

  J_K_Flip_Flop j_k_ff_1 (.J(IEN_J), .clk(Clock), .K(IEN_K), .Q(IEN));  // open: Qn, preset, en, reset

  // Notes on the sheet:
  //   Bu Proje Sakarya Uygulamalı Bilimler Üniversitesi 
  //   Bilgisayar Mühendisliği Öğrencisi Furkan Duran Tarafından Yapılmıştır.
  //   İletişime geçmek için b210109048@subu.edu.tr mail adresini kullanabilirsiniz
endmodule

module FGI_FGO_IEN_Controller (
  input  [2:0] T,
  input  [15:0] IR,
  input  R,
  output FGO_K,
  output FGI_K,
  output IEN_K,
  output IEN_J,
  output FGO_J
);

  wire and_3_out, and_4_out, decoder_1_out2, decoder_1_out3, decoder_2_out7, p;

  Decoder #(.select(3), .enable("false")) decoder_1 (
    .out0(FGO_J), .out2(decoder_1_out2), .out3(decoder_1_out3), .sel(T));  // open: out1, out4, out5, out6, out7
  Decoder #(.select(3), .enable("false")) decoder_2 (
    .out7(decoder_2_out7), .sel(IR[14:12]));  // open: out0, out1, out2, out3, out4, out5, out6
  and and_1 (p, decoder_2_out7, IR[15], decoder_1_out3);
  and and_2 (FGI_K, p, IR[11]);
  and and_3 (and_3_out, decoder_1_out2, R);
  and and_4 (and_4_out, IR[6], p);
  and and_5 (IEN_J, p, IR[7]);
  and and_6 (FGO_K, p, IR[10]);
  or or_1 (IEN_K, and_3_out, and_4_out);

  // Other names for the same wires on the sheet: B6 = IR[6]; B7 = IR[7]; B10 = IR[10]; B11 = IR[11]

  // Notes on the sheet:
  //   Bu Proje Sakarya Uygulamalı Bilimler Üniversitesi 
  //   Bilgisayar Mühendisliği Öğrencisi Furkan Duran Tarafından Yapılmıştır.
  //   İletişime geçmek için b210109048@subu.edu.tr mail adresini kullanabilirsiniz
endmodule

module \_1_Aşamalı_Aritmetik_Devre  (
  input  [1:0] S1S0,
  input  Cin,
  input  [15:0] DR,
  input  [15:0] AC,
  output [15:0] out_5,
  output E
);

  wire adder_1_cout, adder_2_cout, adder_3_cout, adder_4_cout, adder_5_cout, adder_6_cout, adder_7_cout,
       adder_8_cout, adder_9_cout, adder_10_cout, adder_11_cout, adder_12_cout, adder_13_cout, adder_14_cout,
       adder_15_cout, multiplexer_1_out, multiplexer_2_out, multiplexer_3_out, multiplexer_4_out,
       multiplexer_5_out, multiplexer_6_out, multiplexer_7_out, multiplexer_8_out, multiplexer_9_out,
       multiplexer_10_out, multiplexer_11_out, multiplexer_12_out, multiplexer_13_out, multiplexer_14_out,
       multiplexer_15_out, multiplexer_16_out, not_1_out, not_2_out, not_3_out, not_4_out, not_5_out,
       not_6_out, not_7_out, not_8_out, not_9_out, not_10_out, not_11_out, not_12_out, not_13_out,
       not_14_out, not_15_out, not_16_out, not_17_out;

  not not_1 (not_1_out, 1'b0);
  not not_2 (not_2_out, AC[0]);
  Multiplexer #(.select(2), .enable("false")) multiplexer_1 (
    .in0(AC[0]), .in1(not_2_out), .in2(1'b0), .in3(not_1_out), .out(multiplexer_1_out), .sel(S1S0));
  not not_3 (not_3_out, AC[1]);
  Multiplexer #(.select(2), .enable("false")) multiplexer_2 (
    .in0(AC[1]), .in1(not_3_out), .in2(1'b0), .in3(not_1_out), .out(multiplexer_2_out), .sel(S1S0));
  not not_4 (not_4_out, AC[2]);
  Multiplexer #(.select(2), .enable("false")) multiplexer_3 (
    .in0(AC[2]), .in1(not_4_out), .in2(1'b0), .in3(not_1_out), .out(multiplexer_3_out), .sel(S1S0));
  not not_5 (not_5_out, AC[3]);
  Multiplexer #(.select(2), .enable("false")) multiplexer_4 (
    .in0(AC[3]), .in1(not_5_out), .in2(1'b0), .in3(not_1_out), .out(multiplexer_4_out), .sel(S1S0));
  not not_6 (not_6_out, AC[4]);
  Multiplexer #(.select(2), .enable("false")) multiplexer_5 (
    .in0(AC[4]), .in1(not_6_out), .in2(1'b0), .in3(not_1_out), .out(multiplexer_5_out), .sel(S1S0));
  not not_7 (not_7_out, AC[5]);
  Multiplexer #(.select(2), .enable("false")) multiplexer_6 (
    .in0(AC[5]), .in1(not_7_out), .in2(1'b0), .in3(not_1_out), .out(multiplexer_6_out), .sel(S1S0));
  not not_8 (not_8_out, AC[6]);
  Multiplexer #(.select(2), .enable("false")) multiplexer_7 (
    .in0(AC[6]), .in1(not_8_out), .in2(1'b0), .in3(not_1_out), .out(multiplexer_7_out), .sel(S1S0));
  not not_9 (not_9_out, AC[7]);
  Multiplexer #(.select(2), .enable("false")) multiplexer_8 (
    .in0(AC[7]), .in1(not_9_out), .in2(1'b0), .in3(not_1_out), .out(multiplexer_8_out), .sel(S1S0));
  not not_10 (not_10_out, AC[8]);
  Multiplexer #(.select(2), .enable("false")) multiplexer_9 (
    .in0(AC[8]), .in1(not_10_out), .in2(1'b0), .in3(not_1_out), .out(multiplexer_9_out), .sel(S1S0));
  not not_11 (not_11_out, AC[9]);
  Multiplexer #(.select(2), .enable("false")) multiplexer_10 (
    .in0(AC[9]), .in1(not_11_out), .in2(1'b0), .in3(not_1_out), .out(multiplexer_10_out), .sel(S1S0));
  not not_12 (not_12_out, AC[10]);
  Multiplexer #(.select(2), .enable("false")) multiplexer_11 (
    .in0(AC[10]), .in1(not_12_out), .in2(1'b0), .in3(not_1_out), .out(multiplexer_11_out), .sel(S1S0));
  not not_13 (not_13_out, AC[11]);
  Multiplexer #(.select(2), .enable("false")) multiplexer_12 (
    .in0(AC[11]), .in1(not_13_out), .in2(1'b0), .in3(not_1_out), .out(multiplexer_12_out), .sel(S1S0));
  not not_14 (not_14_out, AC[12]);
  Multiplexer #(.select(2), .enable("false")) multiplexer_13 (
    .in0(AC[12]), .in1(not_14_out), .in2(1'b0), .in3(not_1_out), .out(multiplexer_13_out), .sel(S1S0));
  not not_15 (not_15_out, AC[13]);
  Multiplexer #(.select(2), .enable("false")) multiplexer_14 (
    .in0(AC[13]), .in1(not_15_out), .in2(1'b0), .in3(not_1_out), .out(multiplexer_14_out), .sel(S1S0));
  not not_16 (not_16_out, AC[14]);
  Multiplexer #(.select(2), .enable("false")) multiplexer_15 (
    .in0(AC[14]), .in1(not_16_out), .in2(1'b0), .in3(not_1_out), .out(multiplexer_15_out), .sel(S1S0));
  not not_17 (not_17_out, AC[15]);
  Multiplexer #(.select(2), .enable("false")) multiplexer_16 (
    .in0(AC[15]), .in1(not_17_out), .in2(1'b0), .in3(not_1_out), .out(multiplexer_16_out), .sel(S1S0));
  Adder #(.width(1)) adder_1 (.a(DR[0]), .b(multiplexer_1_out), .out(out_5[0]), .cin(Cin), .cout(adder_1_cout));
  Adder #(.width(1)) adder_2 (
    .a(DR[1]), .b(multiplexer_2_out), .out(out_5[1]), .cin(adder_1_cout), .cout(adder_2_cout));
  Adder #(.width(1)) adder_3 (
    .a(DR[2]), .b(multiplexer_3_out), .out(out_5[2]), .cin(adder_2_cout), .cout(adder_3_cout));
  Adder #(.width(1)) adder_4 (
    .a(DR[3]), .b(multiplexer_4_out), .out(out_5[3]), .cin(adder_3_cout), .cout(adder_4_cout));
  Adder #(.width(1)) adder_5 (
    .a(DR[4]), .b(multiplexer_5_out), .out(out_5[4]), .cin(adder_4_cout), .cout(adder_5_cout));
  Adder #(.width(1)) adder_6 (
    .a(DR[5]), .b(multiplexer_6_out), .out(out_5[5]), .cin(adder_5_cout), .cout(adder_6_cout));
  Adder #(.width(1)) adder_7 (
    .a(DR[6]), .b(multiplexer_7_out), .out(out_5[6]), .cin(adder_6_cout), .cout(adder_7_cout));
  Adder #(.width(1)) adder_8 (
    .a(DR[7]), .b(multiplexer_8_out), .out(out_5[7]), .cin(adder_7_cout), .cout(adder_8_cout));
  Adder #(.width(1)) adder_9 (
    .a(DR[8]), .b(multiplexer_9_out), .out(out_5[8]), .cin(adder_8_cout), .cout(adder_9_cout));
  Adder #(.width(1)) adder_10 (
    .a(DR[9]), .b(multiplexer_10_out), .out(out_5[9]), .cin(adder_9_cout), .cout(adder_10_cout));
  Adder #(.width(1)) adder_11 (
    .a(DR[10]), .b(multiplexer_11_out), .out(out_5[10]), .cin(adder_10_cout), .cout(adder_11_cout));
  Adder #(.width(1)) adder_12 (
    .a(DR[11]), .b(multiplexer_12_out), .out(out_5[11]), .cin(adder_11_cout), .cout(adder_12_cout));
  Adder #(.width(1)) adder_13 (
    .a(DR[12]), .b(multiplexer_13_out), .out(out_5[12]), .cin(adder_12_cout), .cout(adder_13_cout));
  Adder #(.width(1)) adder_14 (
    .a(DR[13]), .b(multiplexer_14_out), .out(out_5[13]), .cin(adder_13_cout), .cout(adder_14_cout));
  Adder #(.width(1)) adder_15 (
    .a(DR[14]), .b(multiplexer_15_out), .out(out_5[14]), .cin(adder_14_cout), .cout(adder_15_cout));
  Adder #(.width(1)) adder_16 (.a(DR[15]), .b(multiplexer_16_out), .out(out_5[15]), .cin(adder_15_cout), .cout(E));

  // Notes on the sheet:
  //   Bu Proje Sakarya Uygulamalı Bilimler Üniversitesi 
  //   Bilgisayar Mühendisliği Öğrencisi Furkan Duran Tarafından Yapılmıştır.
  //   İletişime geçmek için b210109048@subu.edu.tr mail adresini kullanabilirsiniz
endmodule

module \_1_Aşamalı_Mantık_Devresi  (
  input  [1:0] S1S0,
  input  [15:0] input_1,
  input  [15:0] input_2,
  output [15:0] out_4
);

  wire and_1_out, and_2_out, and_3_out, and_4_out, and_5_out, and_6_out, and_7_out, and_8_out, and_9_out,
       and_10_out, and_11_out, and_12_out, and_13_out, and_14_out, and_15_out, and_16_out, not_1_out,
       not_2_out, not_3_out, not_4_out, not_5_out, not_6_out, not_7_out, not_8_out, not_9_out, not_10_out,
       not_11_out, not_12_out, not_13_out, not_14_out, not_15_out, not_16_out, or_1_out, or_2_out, or_3_out,
       or_4_out, or_5_out, or_6_out, or_7_out, or_8_out, or_9_out, or_10_out, or_11_out, or_12_out,
       or_13_out, or_14_out, or_15_out, or_16_out, xor_1_out, xor_2_out, xor_3_out, xor_4_out, xor_5_out,
       xor_6_out, xor_7_out, xor_8_out, xor_9_out, xor_10_out, xor_11_out, xor_12_out, xor_13_out,
       xor_14_out, xor_15_out, xor_16_out;

  and and_1 (and_1_out, input_1[0], input_2[0]);
  or or_1 (or_1_out, input_1[0], input_2[0]);
  xor xor_1 (xor_1_out, input_1[0], input_2[0]);
  not not_1 (not_1_out, input_1[0]);
  and and_2 (and_2_out, input_1[1], input_2[1]);
  or or_2 (or_2_out, input_1[1], input_2[1]);
  xor xor_2 (xor_2_out, input_1[1], input_2[1]);
  not not_2 (not_2_out, input_1[1]);
  and and_3 (and_3_out, input_1[2], input_2[2]);
  or or_3 (or_3_out, input_1[2], input_2[2]);
  xor xor_3 (xor_3_out, input_1[2], input_2[2]);
  not not_3 (not_3_out, input_1[2]);
  and and_4 (and_4_out, input_1[3], input_2[3]);
  or or_4 (or_4_out, input_1[3], input_2[3]);
  xor xor_4 (xor_4_out, input_1[3], input_2[3]);
  not not_4 (not_4_out, input_1[3]);
  and and_5 (and_5_out, input_1[4], input_2[4]);
  or or_5 (or_5_out, input_1[4], input_2[4]);
  xor xor_5 (xor_5_out, input_1[4], input_2[4]);
  not not_5 (not_5_out, input_1[4]);
  and and_6 (and_6_out, input_1[5], input_2[5]);
  or or_6 (or_6_out, input_1[5], input_2[5]);
  xor xor_6 (xor_6_out, input_1[5], input_2[5]);
  not not_6 (not_6_out, input_1[5]);
  and and_7 (and_7_out, input_1[6], input_2[6]);
  or or_7 (or_7_out, input_1[6], input_2[6]);
  xor xor_7 (xor_7_out, input_1[6], input_2[6]);
  not not_7 (not_7_out, input_1[6]);
  and and_8 (and_8_out, input_1[7], input_2[7]);
  or or_8 (or_8_out, input_1[7], input_2[7]);
  xor xor_8 (xor_8_out, input_1[7], input_2[7]);
  not not_8 (not_8_out, input_1[7]);
  Multiplexer #(.select(2)) multiplexer_1 (
    .in0(and_1_out), .in1(or_1_out), .in2(xor_1_out), .in3(not_1_out), .out(out_4[0]), .sel(S1S0), .en(1'b1));
  Multiplexer #(.select(2)) multiplexer_2 (
    .in0(and_2_out), .in1(or_2_out), .in2(xor_2_out), .in3(not_2_out), .out(out_4[1]), .sel(S1S0), .en(1'b1));
  Multiplexer #(.select(2)) multiplexer_3 (
    .in0(and_3_out), .in1(or_3_out), .in2(xor_3_out), .in3(not_3_out), .out(out_4[2]), .sel(S1S0), .en(1'b1));
  Multiplexer #(.select(2)) multiplexer_4 (
    .in0(and_4_out), .in1(or_4_out), .in2(xor_4_out), .in3(not_4_out), .out(out_4[3]), .sel(S1S0), .en(1'b1));
  Multiplexer #(.select(2)) multiplexer_5 (
    .in0(and_5_out), .in1(or_5_out), .in2(xor_5_out), .in3(not_5_out), .out(out_4[4]), .sel(S1S0), .en(1'b1));
  Multiplexer #(.select(2)) multiplexer_6 (
    .in0(and_6_out), .in1(or_6_out), .in2(xor_6_out), .in3(not_6_out), .out(out_4[5]), .sel(S1S0), .en(1'b1));
  Multiplexer #(.select(2)) multiplexer_7 (
    .in0(and_7_out), .in1(or_7_out), .in2(xor_7_out), .in3(not_7_out), .out(out_4[6]), .sel(S1S0), .en(1'b1));
  Multiplexer #(.select(2)) multiplexer_8 (
    .in0(and_8_out), .in1(or_8_out), .in2(xor_8_out), .in3(not_8_out), .out(out_4[7]), .sel(S1S0), .en(1'b1));
  and and_9 (and_9_out, input_1[8], input_2[8]);
  or or_9 (or_9_out, input_1[8], input_2[8]);
  xor xor_9 (xor_9_out, input_1[8], input_2[8]);
  not not_9 (not_9_out, input_1[8]);
  and and_10 (and_10_out, input_1[9], input_2[9]);
  or or_10 (or_10_out, input_1[9], input_2[9]);
  xor xor_10 (xor_10_out, input_1[9], input_2[9]);
  not not_10 (not_10_out, input_1[9]);
  and and_11 (and_11_out, input_1[10], input_2[10]);
  or or_11 (or_11_out, input_1[10], input_2[10]);
  xor xor_11 (xor_11_out, input_1[10], input_2[10]);
  not not_11 (not_11_out, input_1[10]);
  and and_12 (and_12_out, input_1[11], input_2[11]);
  or or_12 (or_12_out, input_1[11], input_2[11]);
  xor xor_12 (xor_12_out, input_1[11], input_2[11]);
  not not_12 (not_12_out, input_1[11]);
  and and_13 (and_13_out, input_1[12], input_2[12]);
  or or_13 (or_13_out, input_1[12], input_2[12]);
  xor xor_13 (xor_13_out, input_1[12], input_2[12]);
  not not_13 (not_13_out, input_1[12]);
  and and_14 (and_14_out, input_1[13], input_2[13]);
  or or_14 (or_14_out, input_1[13], input_2[13]);
  xor xor_14 (xor_14_out, input_1[13], input_2[13]);
  not not_14 (not_14_out, input_1[13]);
  and and_15 (and_15_out, input_1[14], input_2[14]);
  or or_15 (or_15_out, input_1[14], input_2[14]);
  xor xor_15 (xor_15_out, input_1[14], input_2[14]);
  not not_15 (not_15_out, input_1[14]);
  and and_16 (and_16_out, input_1[15], input_2[15]);
  or or_16 (or_16_out, input_1[15], input_2[15]);
  xor xor_16 (xor_16_out, input_1[15], input_2[15]);
  not not_16 (not_16_out, input_1[15]);
  Multiplexer #(.select(2)) multiplexer_9 (
    .in0(and_9_out), .in1(or_9_out), .in2(xor_9_out), .in3(not_9_out), .out(out_4[8]), .sel(S1S0), .en(1'b1));
  Multiplexer #(.select(2)) multiplexer_10 (
    .in0(and_10_out), .in1(or_10_out), .in2(xor_10_out), .in3(not_10_out), .out(out_4[9]), .sel(S1S0),
    .en(1'b1));
  Multiplexer #(.select(2)) multiplexer_11 (
    .in0(and_11_out), .in1(or_11_out), .in2(xor_11_out), .in3(not_11_out), .out(out_4[10]), .sel(S1S0),
    .en(1'b1));
  Multiplexer #(.select(2)) multiplexer_12 (
    .in0(and_12_out), .in1(or_12_out), .in2(xor_12_out), .in3(not_12_out), .out(out_4[11]), .sel(S1S0),
    .en(1'b1));
  Multiplexer #(.select(2)) multiplexer_13 (
    .in0(and_13_out), .in1(or_13_out), .in2(xor_13_out), .in3(not_13_out), .out(out_4[12]), .sel(S1S0),
    .en(1'b1));
  Multiplexer #(.select(2)) multiplexer_14 (
    .in0(and_14_out), .in1(or_14_out), .in2(xor_14_out), .in3(not_14_out), .out(out_4[13]), .sel(S1S0),
    .en(1'b1));
  Multiplexer #(.select(2)) multiplexer_15 (
    .in0(and_15_out), .in1(or_15_out), .in2(xor_15_out), .in3(not_15_out), .out(out_4[14]), .sel(S1S0),
    .en(1'b1));
  Multiplexer #(.select(2)) multiplexer_16 (
    .in0(and_16_out), .in1(or_16_out), .in2(xor_16_out), .in3(not_16_out), .out(out_4[15]), .sel(S1S0),
    .en(1'b1));

  // Notes on the sheet:
  //   Bu Proje Sakarya Uygulamalı Bilimler Üniversitesi 
  //   Bilgisayar Mühendisliği Öğrencisi Furkan Duran Tarafından Yapılmıştır.
  //   İletişime geçmek için b210109048@subu.edu.tr mail adresini kullanabilirsiniz
endmodule

module \Aritmetik_Mantık_Kaydırma_Birimi  (
  input  [3:0] S3S2S1S0,
  input  Cin,
  input  [15:0] DR,
  input  [15:0] AC,
  output E,
  output [15:0] ALU_OUT
);

  wire [15:0] \kaydırma_1_out_3 , \n1_aşamalı_aritmetik_devre_1_out_5 , \n1_aşamalı_mantık_devresi_1_out_4 ;

  \_1_Aşamalı_Aritmetik_Devre  \u_1_aşamalı_aritmetik_devre_1  (
    .DR(DR), .AC(AC), .S1S0(S3S2S1S0[1:0]), .Cin(Cin), .E(E), .out_5(\n1_aşamalı_aritmetik_devre_1_out_5 ));
  \_1_Aşamalı_Mantık_Devresi  \u_1_aşamalı_mantık_devresi_1  (
    .S1S0(S3S2S1S0[1:0]), .input_1(AC), .input_2(DR), .out_4(\n1_aşamalı_mantık_devresi_1_out_4 ));
  Multiplexer #(.select(2), .width(16), .enable("false")) multiplexer_1 (
    .in0(\n1_aşamalı_aritmetik_devre_1_out_5 ), .in1(\n1_aşamalı_mantık_devresi_1_out_4 ),
    .in2(\kaydırma_1_out_3 ), .in3(\kaydırma_1_out_3 ), .out(ALU_OUT), .sel(S3S2S1S0[3:2]));
  \Kaydırma  \kaydırma_1  (.\Seçim_1__Sağa_0___Sola (S3S2S1S0[2]), .AC(AC), .out_3(\kaydırma_1_out_3 ));

  // Notes on the sheet:
  //   Bu Proje Sakarya Uygulamalı Bilimler Üniversitesi 
  //   ALU İŞLEMLER SEÇİM UÇLARI
  //   S3    S2    S1    S0    Cin
  //   ------------------------------------
  //   0       0      0      0        0
  //   0       0      0      0        1
  //   0       0      0      1        0
  //   0       0      0      1        1
  //   0       0      1      0        0
  //   0       0      1      0        1
  //   0       0      1      1        0
  //   0       0      1      1        1
  //   0       1      0      0        0
  //   0       1      0      1        0
  //   0       0      1      1        0
  //   0       1      1      1        0
  //   1       0      0      0        0
  //   1       1      0      0        0
  //   Bilgisayar Mühendisliği Öğrencisi Furkan Duran Tarafından Yapılmıştır.
  //   İletişime geçmek için b210109048@subu.edu.tr mail adresini kullanabilirsiniz
  //   F = DR + AC
  //   F = DR + AC + 1 
  //   F = DR + AC'
  //   F = DR         
  //   F = DR + 1
  //   F = DR -1
  //   F = DR
  //   F = DR ∧ AC
  //   F = DR v AC
  //   F = DR ⊕ AC
  //   F = AC'
  //   F = shl AC
  //   F = shr AC
  //   F = DR + AC' + 1      (DR-AC) 
endmodule

module \Kaydırma  (
  input  \Seçim_1__Sağa_0___Sola ,
  input  [15:0] AC,
  output [15:0] out_3
);

  Multiplexer multiplexer_1 (.in0(1'b0), .in1(AC[1]), .out(out_3[0]), .sel(\Seçim_1__Sağa_0___Sola ), .en(1'b1));
  Multiplexer multiplexer_2 (.in0(AC[0]), .in1(AC[2]), .out(out_3[1]), .sel(\Seçim_1__Sağa_0___Sola ), .en(1'b1));
  Multiplexer multiplexer_3 (.in0(AC[1]), .in1(AC[3]), .out(out_3[2]), .sel(\Seçim_1__Sağa_0___Sola ), .en(1'b1));
  Multiplexer multiplexer_4 (.in0(AC[2]), .in1(AC[4]), .out(out_3[3]), .sel(\Seçim_1__Sağa_0___Sola ), .en(1'b1));
  Multiplexer multiplexer_5 (.in0(AC[3]), .in1(AC[5]), .out(out_3[4]), .sel(\Seçim_1__Sağa_0___Sola ), .en(1'b1));
  Multiplexer multiplexer_6 (.in0(AC[4]), .in1(AC[6]), .out(out_3[5]), .sel(\Seçim_1__Sağa_0___Sola ), .en(1'b1));
  Multiplexer multiplexer_7 (.in0(AC[5]), .in1(AC[7]), .out(out_3[6]), .sel(\Seçim_1__Sağa_0___Sola ), .en(1'b1));
  Multiplexer multiplexer_8 (.in0(AC[6]), .in1(AC[8]), .out(out_3[7]), .sel(\Seçim_1__Sağa_0___Sola ), .en(1'b1));
  Multiplexer multiplexer_9 (.in0(AC[7]), .in1(AC[9]), .out(out_3[8]), .sel(\Seçim_1__Sağa_0___Sola ), .en(1'b1));
  Multiplexer multiplexer_10 (.in0(AC[8]), .in1(AC[10]), .out(out_3[9]), .sel(\Seçim_1__Sağa_0___Sola ), .en(1'b1));
  Multiplexer multiplexer_11 (.in0(AC[9]), .in1(AC[11]), .out(out_3[10]), .sel(\Seçim_1__Sağa_0___Sola ), .en(1'b1));
  Multiplexer multiplexer_12 (.in0(AC[10]), .in1(AC[12]), .out(out_3[11]), .sel(\Seçim_1__Sağa_0___Sola ), .en(1'b1));
  Multiplexer multiplexer_13 (.in0(AC[11]), .in1(AC[13]), .out(out_3[12]), .sel(\Seçim_1__Sağa_0___Sola ), .en(1'b1));
  Multiplexer multiplexer_14 (.in0(AC[12]), .in1(AC[14]), .out(out_3[13]), .sel(\Seçim_1__Sağa_0___Sola ), .en(1'b1));
  Multiplexer multiplexer_15 (.in0(AC[13]), .in1(AC[15]), .out(out_3[14]), .sel(\Seçim_1__Sağa_0___Sola ), .en(1'b1));
  Multiplexer multiplexer_16 (.in0(AC[14]), .in1(1'b0), .out(out_3[15]), .sel(\Seçim_1__Sağa_0___Sola ), .en(1'b1));

  // Notes on the sheet:
  //   Bu Proje Sakarya Uygulamalı Bilimler Üniversitesi 
  //   Bilgisayar Mühendisliği Öğrencisi Furkan Duran Tarafından Yapılmıştır.
  //   İletişime geçmek için b210109048@subu.edu.tr mail adresini kullanabilirsiniz
endmodule

module ALU (
  input  [2:0] T,
  input  [15:0] IR,
  input  E_in,
  input  [15:0] DR,
  input  [15:0] AC,
  output E_out,
  output [15:0] AC_Entiry
);

  wire and_3_out, and_4_out, and_5_out, and_6_out, and_7_out, and_8_out, decoder_1_out3, decoder_1_out5,
       decoder_2_out0, decoder_2_out1, decoder_2_out2, decoder_2_out7, not_1_out, or_1_out, or_2_out, p, r;
  wire [3:0] Select;

  \Aritmetik_Mantık_Kaydırma_Birimi  \aritmetik_mantık_kaydırma_birimi_1  (
    .S3S2S1S0(Select), .DR(DR), .AC(AC), .E(E_out), .ALU_OUT(AC_Entiry), .Cin(E_in));
  Decoder #(.select(3), .enable("false")) decoder_1 (
    .out3(decoder_1_out3), .out5(decoder_1_out5), .sel(T));  // open: out0, out1, out2, out4, out6, out7
  Decoder #(.select(3), .enable("false")) decoder_2 (
    .out0(decoder_2_out0), .out1(decoder_2_out1), .out2(decoder_2_out2), .out7(decoder_2_out7),
    .sel(IR[14:12]));  // open: out3, out4, out5, out6
  and and_1 (r, decoder_2_out7, ~IR[15], decoder_1_out3);  // AND_Gate
  and and_2 (p, decoder_2_out7, IR[15], decoder_1_out3);
  or or_1 (or_1_out, and_3_out, and_4_out, and_5_out, and_6_out, and_7_out, and_8_out);
  and and_3 (and_3_out, decoder_2_out0, decoder_1_out5);
  and and_4 (and_4_out, decoder_2_out1, decoder_1_out5);
  and and_5 (and_5_out, decoder_2_out2, decoder_1_out5);
  and and_6 (and_6_out, IR[9], r);
  and and_7 (and_7_out, IR[7], r);
  and and_8 (and_8_out, IR[6], r);
  not not_1 (not_1_out, or_1_out);
  or or_2 (or_2_out, not_1_out, and_5_out);
  Priority_Encoder #(.select(4)) priority_encoder_1 (
    .in0(and_4_out), .in2(or_2_out), .in4(and_3_out), .in7(and_6_out), .in8(and_8_out), .in12(and_7_out),
    .out(Select));  // open: in1, in3, in5, in6, in9, in10, in11, in13, in14, in15, gs, en_out, en_in

  // Notes on the sheet:
  //   Bu Proje Sakarya Uygulamalı Bilimler Üniversitesi 
  //   Bilgisayar Mühendisliği Öğrencisi Furkan Duran Tarafından Yapılmıştır.
  //   İletişime geçmek için b210109048@subu.edu.tr mail adresini kullanabilirsiniz
  //   Bir nevi AC giriş
  //   İşlemler için gelen AND kapıları
  //   ------------------------------------
  //   1.AND = D0T5        AC <-  AC ∧ DR
  //   2.AND =  D1T5       AC <- AC + DR
  //   3.AND =  D2T5     AC <- DR
  //   4.AND =  rB(9)     AC <- AC'
  //   5.AND =  rB(7)     AC <- shr AC
  //   6.AND =  rB(6)     AC <- shl AC
endmodule
module BUS_Select (
  input  [15:0] IR,
  input  [2:0] T,
  input  R,
  output [2:0] Bus_Select
);

  wire and_2_out, and_3_out, and_4_out, and_5_out, and_6_out, and_7_out, and_8_out, and_9_out, and_10_out,
       and_11_out, and_12_out, and_13_out, and_14_out, decoder_1_out0, decoder_1_out1, decoder_1_out2,
       decoder_1_out3, decoder_1_out4, decoder_1_out5, decoder_1_out6, decoder_2_out0, decoder_2_out1,
       decoder_2_out2, decoder_2_out3, decoder_2_out4, decoder_2_out5, decoder_2_out6, decoder_2_out7,
       or_1_out, or_2_out, or_3_out, or_4_out, or_5_out, or_6_out, p;
  wire [2:0] priority_encoder_1_out;

  Decoder #(.select(3), .enable("false")) decoder_1 (
    .out0(decoder_1_out0), .out1(decoder_1_out1), .out2(decoder_1_out2), .out3(decoder_1_out3),
    .out4(decoder_1_out4), .out5(decoder_1_out5), .out6(decoder_1_out6), .sel(T));  // open: out7
  Decoder #(.select(3), .enable("false")) decoder_2 (
    .out0(decoder_2_out0), .out1(decoder_2_out1), .out2(decoder_2_out2), .out3(decoder_2_out3),
    .out4(decoder_2_out4), .out5(decoder_2_out5), .out6(decoder_2_out6), .out7(decoder_2_out7),
    .sel(IR[14:12]));
  and and_1 (p, decoder_2_out7, IR[15], decoder_1_out3);
  and and_2 (and_2_out, decoder_2_out5, decoder_1_out4);
  and and_3 (and_3_out, decoder_1_out4, decoder_2_out4);
  and and_4 (and_4_out, decoder_2_out5, decoder_1_out5);
  and and_5 (and_5_out, decoder_2_out6, decoder_1_out6);
  and and_6 (and_6_out, decoder_2_out2, decoder_1_out5);
  and and_7 (and_7_out, decoder_2_out3, decoder_1_out4);
  and and_8 (and_8_out, IR[10], p);
  and and_9 (and_9_out, decoder_1_out2, ~R);  // AND_Gate
  and and_10 (and_10_out, decoder_1_out1, R);
  and and_11 (and_11_out, decoder_1_out1, ~R);  // AND_Gate
  and and_12 (and_12_out, ~decoder_2_out7, IR[15], decoder_1_out3);  // AND_Gate
  or or_1 (or_1_out, decoder_2_out0, decoder_2_out1, decoder_2_out2, decoder_2_out6);
  or or_2 (or_2_out, decoder_1_out0, and_2_out);
  or or_3 (or_3_out, and_3_out, and_4_out);
  or or_4 (or_4_out, and_5_out, and_6_out);
  or or_5 (or_5_out, and_7_out, and_8_out);
  and and_13 (and_13_out, or_1_out, decoder_1_out4);
  or or_6 (or_6_out, and_11_out, and_12_out, and_13_out);
  and and_14 (and_14_out, ~or_3_out, ~or_2_out, ~or_4_out, ~or_5_out, ~and_9_out, ~and_10_out, ~or_6_out);  // AND_Gate
  Priority_Encoder priority_encoder_1 (
    .in0(and_14_out), .in1(or_3_out), .in2(or_2_out), .in3(or_4_out), .in4(or_5_out), .in5(and_9_out),
    .in6(and_10_out), .in7(or_6_out), .out(priority_encoder_1_out));  // open: en_in, gs, en_out
  Multiplexer #(.select(3), .width(3), .enable("false")) multiplexer_1 (
    .in0(3'b000), .in1(3'b001), .in2(3'b010), .in3(3'b011), .in4(3'b100), .in5(3'b101), .in6(3'b110),
    .in7(3'b111), .out(Bus_Select), .sel(priority_encoder_1_out));

  // Notes on the sheet:
  //   T0
  //   D5T4
  //   D4T4
  //   D5T5
  //   D6T6
  //   D2T5
  //   D3T4
  //   D7IT3R'
  //   R'T2
  //   RT1
  //   R'T1
  //   D7'T3I
  //   D0+D1+D2+D6
  //   T4
  //   T3D7I
  //   AR<-PC
  //   PC<-AR
  //   D0T4+D1T4+D2T4+D6T4
  //   BUS BOŞTA
  //   ENCODER
  //   ----------
  //   0 için Sitem Çalışmazken 
  //   1 için AR ' YE ORTAK YOLU AÇAR
  //   2 için PC ' YE ORTAK YOLU AÇAR
  //   3 için DR ' YE ORTAK YOLU AÇAR
  //   4 için AC ' YE ORTAK YOLU AÇAR
  //   5 için IR ' YE ORTAK YOLU AÇAR
  //   6 için TR ' YE ORTAK YOLU AÇAR
  //   7 için RAM ' E ORTAK YOLU AÇAR
  //   Bu Proje Sakarya Uygulamalı Bilimler Üniversitesi 
  //   Bilgisayar Mühendisliği Öğrencisi Furkan Duran Tarafından Yapılmıştır.
  //   İletişime geçmek için b210109048@subu.edu.tr mail adresini kullanabilirsiniz
endmodule
